// Logisim project cannonGame.circ as structural Verilog: 11 circuits, main circuit main
module main (
);

  wire button_1_out, c, cannonmov_1_fire, cannonmov_1_tilt;
  wire [3:0] movement_1_score0, movement_1_score1;
  wire [6:0] keyboard_1_data;
  wire [31:0] cannonmov_1_basepos, cannonmov_1_cannonpos, movement_1_out_9, movement_1_out_10,
       movement_1_out_11, movement_1_out_12, movement_1_out_13, movement_1_out_14, movement_1_out_15,
       movement_1_out_16, movement_1_out_17, movement_1_out_18, movement_1_out_19, movement_1_out_20,
       movement_1_out_21, movement_1_out_22, movement_1_out_23, movement_1_out_24, movement_1_out_25,
       movement_1_out_26, movement_1_out_27, movement_1_out_28, movement_1_out_29, movement_1_out_30,
       movement_1_out_31, movement_1_out_32, movement_1_out_33, movement_1_out_34, movement_1_out_35,
       movement_1_out_36, movement_1_out_37, movement_1_out_38, movement_1_out_39, movement_1_out_40;

  Clock clock_1 (.out(c));
  Keyboard keyboard_1 (.clk(c), .data(keyboard_1_data));  // open: re, clr, avail
  Button button_1 (.out(button_1_out));
  cannonMov cannonmov_1 (
    .in_1(keyboard_1_data), .Reset(button_1_out), .BasePos(cannonmov_1_basepos),
    .CannonPos(cannonmov_1_cannonpos), .Tilt(cannonmov_1_tilt), .Fire(cannonmov_1_fire));
  Hex_Digit_Display hex_digit_display_1 (.value(movement_1_score1));  // open: dp
  DotMatrix #(.inputtype("row"), .matrixcols(32), .matrixrows(32)) dotmatrix_1 (
    .row0(movement_1_out_9), .row1(movement_1_out_10), .row2(movement_1_out_11), .row3(movement_1_out_12),
    .row4(movement_1_out_13), .row5(movement_1_out_14), .row6(movement_1_out_15), .row7(movement_1_out_16),
    .row8(movement_1_out_17), .row9(movement_1_out_18), .row10(movement_1_out_19), .row11(movement_1_out_20),
    .row12(movement_1_out_21), .row13(movement_1_out_22), .row14(movement_1_out_23),
    .row15(movement_1_out_24), .row16(movement_1_out_25), .row17(movement_1_out_26),
    .row18(movement_1_out_27), .row19(movement_1_out_28), .row20(movement_1_out_29),
    .row21(movement_1_out_30), .row22(movement_1_out_31), .row23(movement_1_out_32),
    .row24(movement_1_out_33), .row25(movement_1_out_34), .row26(movement_1_out_35),
    .row27(movement_1_out_36), .row28(movement_1_out_37), .row29(movement_1_out_38),
    .row30(movement_1_out_39), .row31(movement_1_out_40));
  movement movement_1 (
    .CannonPos(cannonmov_1_cannonpos), .BasePos(cannonmov_1_basepos), .Fire(cannonmov_1_fire),
    .Tilt(cannonmov_1_tilt), .Reset(button_1_out), .Clock(c), .score1(movement_1_score1),
    .score0(movement_1_score0), .out_9(movement_1_out_9), .out_10(movement_1_out_10),
    .out_11(movement_1_out_11), .out_12(movement_1_out_12), .out_13(movement_1_out_13),
    .out_14(movement_1_out_14), .out_15(movement_1_out_15), .out_16(movement_1_out_16),
    .out_17(movement_1_out_17), .out_18(movement_1_out_18), .out_19(movement_1_out_19),
    .out_20(movement_1_out_20), .out_21(movement_1_out_21), .out_22(movement_1_out_22),
    .out_23(movement_1_out_23), .out_24(movement_1_out_24), .out_25(movement_1_out_25),
    .out_26(movement_1_out_26), .out_27(movement_1_out_27), .out_28(movement_1_out_28),
    .out_29(movement_1_out_29), .out_30(movement_1_out_30), .out_31(movement_1_out_31),
    .out_32(movement_1_out_32), .out_33(movement_1_out_33), .out_34(movement_1_out_34),
    .out_35(movement_1_out_35), .out_36(movement_1_out_36), .out_37(movement_1_out_37),
    .out_38(movement_1_out_38), .out_39(movement_1_out_39), .out_40(movement_1_out_40));
  Hex_Digit_Display hex_digit_display_2 (.value(movement_1_score0));  // open: dp

  // Notes on the sheet:
  //   a - Move Left
  //   d - Move Right
  //   q - Tilt Left
  //   e - Tilt Right
  //   Space Bar - Shoot
  //   Press to start/reset
  //   SCORE
endmodule

module keyboard (
  input  [6:0] in_1,
  output out_2,
  output out_3,
  output out_4,
  output Fire
);

  wire clock_1_out, multiplexer_1_out, multiplexer_2_out, not_1_out, or_1_out;
  wire [1:0] comparator_3_eq;

  Comparator #(.width(7)) comparator_1 (.a(in_1), .b(7'b1100001), .eq(out_2));  // open: gt, lt
  Comparator #(.width(7)) comparator_2 (.a(in_1), .b(7'b1100100), .eq(out_3));  // open: gt, lt
  Comparator #(.width(7)) comparator_3 (.a(in_1), .b(7'b1100101), .eq(comparator_3_eq[0]));  // open: gt, lt
  Comparator #(.width(7)) comparator_4 (.a(in_1), .b(7'b1110001), .eq(comparator_3_eq[1]));  // open: gt, lt
  Comparator #(.width(7)) comparator_5 (.a(in_1), .b(7'b0100000), .eq(Fire));  // open: gt, lt
  not not_1 (not_1_out, comparator_3_eq[0]);
  or or_1 (or_1_out, comparator_3_eq[0], comparator_3_eq[1]);
  Multiplexer #(.select(2), .enable("false")) multiplexer_1 (
    .in0(out_4), .in1(comparator_3_eq[1]), .in2(not_1_out), .in3(out_4), .out(multiplexer_1_out),
    .sel(comparator_3_eq));
  Clock clock_1 (.out(clock_1_out));
  Multiplexer #(.enable("false")) multiplexer_2 (
    .in0(out_4), .in1(multiplexer_1_out), .out(multiplexer_2_out), .sel(or_1_out));
  D_Flip_Flop d_ff_1 (.clk(clock_1_out), .D(multiplexer_2_out), .Q(out_4));  // open: Qn, preset, en, reset
endmodule

module cannonMov (
  input  [6:0] in_1,
  input  Reset,
  output [31:0] BasePos,
  output [31:0] CannonPos,
  output Tilt,
  output Fire
);

  wire and_1_out, and_2_out, and_3_out, and_4_out, clock_1_out, comparator_1_eq, comparator_2_eq,
       comparator_3_eq, comparator_4_eq, L, or_1_out, or_2_out, or_3_out, R;
  wire [4:0] adder_1_out, multiplexer_1_out, multiplexer_2_out, multiplexer_3_out, register_1_q,
       subtractor_1_out;
  wire [31:0] shifter_2_out, shifter_3_out;

  keyboard keyboard_1 (.in_1(in_1), .out_2(L), .out_3(R), .out_4(Tilt), .Fire(Fire));
  Subtractor #(.width(5)) subtractor_1 (.a(register_1_q), .b(5'b00001), .out(subtractor_1_out));  // open: bin, bout
  Adder #(.width(5)) adder_1 (.a(5'b00001), .b(register_1_q), .out(adder_1_out));  // open: cin, cout
  Multiplexer #(.select(2), .width(5), .enable("false")) multiplexer_1 (
    .in0(register_1_q), .in1(subtractor_1_out), .in2(adder_1_out), .in3(register_1_q),
    .out(multiplexer_1_out), .sel({L, R}));
  Multiplexer #(.width(5), .enable("false")) multiplexer_2 (
    .in0(multiplexer_3_out), .in1(5'b10000), .out(multiplexer_2_out), .sel(Reset));
  Comparator #(.width(32)) comparator_1 (.a(BasePos), .b(32'h1), .eq(comparator_1_eq));  // open: gt, lt
  Comparator #(.width(32)) comparator_2 (.a(BasePos), .b(32'h80000000), .eq(comparator_2_eq));  // open: gt, lt
  Register #(.width(5)) register_1 (
    .D(multiplexer_2_out), .en(1'b1), .Q(register_1_q), .clk(clock_1_out));  // open: clr
  Clock clock_1 (.out(clock_1_out));
  and and_1 (and_1_out, comparator_1_eq, R);
  or or_1 (or_1_out, and_1_out, and_2_out);
  and and_2 (and_2_out, comparator_2_eq, L);
  Multiplexer #(.width(5), .enable("false")) multiplexer_3 (
    .in0(multiplexer_1_out), .in1(register_1_q), .out(multiplexer_3_out), .sel(or_2_out));
  or or_2 (or_2_out, or_1_out, or_3_out);
  Shifter #(.width(32)) shifter_1 (.in(32'h1), .\dist (register_1_q), .out(BasePos));
  Shifter #(.width(32), .shift("lr")) shifter_2 (.in(BasePos), .\dist (5'b00001), .out(shifter_2_out));
  Shifter #(.width(32)) shifter_3 (.in(BasePos), .\dist (5'b00001), .out(shifter_3_out));
  Multiplexer #(.width(32), .enable("false")) multiplexer_4 (
    .in0(shifter_2_out), .in1(shifter_3_out), .out(CannonPos), .sel(Tilt));
  Comparator #(.width(32)) comparator_3 (.a(CannonPos), .b(32'h1), .eq(comparator_3_eq));  // open: gt, lt
  Comparator #(.width(32)) comparator_4 (.a(CannonPos), .b(32'h80000000), .eq(comparator_4_eq));  // open: gt, lt
  and and_3 (and_3_out, comparator_3_eq, R);
  and and_4 (and_4_out, comparator_4_eq, L);
  or or_3 (or_3_out, and_4_out, and_3_out);
endmodule

module test (
  input  in_1,
  input  in_2,
  input  in_3,
  input  in_4,
  input  in_5,
  input  [31:0] in_6,
  input  [31:0] in_7,
  input  [31:0] in_8,
  input  [31:0] in_9,
  input  [31:0] in_10,
  input  [31:0] in_11,
  input  in_12,
  input  [31:0] in_13,
  input  [31:0] in_14,
  input  [31:0] in_15,
  input  [31:0] in_16,
  input  [31:0] in_17,
  input  [31:0] in_18,
  input  [31:0] in_19,
  input  [31:0] in_20,
  input  [31:0] in_21,
  input  [31:0] in_22,
  input  in_23,
  input  [31:0] in_24,
  input  [31:0] in_25,
  input  [31:0] in_26,
  input  [31:0] in_27,
  input  [31:0] in_28,
  input  [31:0] in_29,
  input  [31:0] in_30,
  input  [31:0] in_31,
  input  [31:0] in_32,
  input  [31:0] gUpSubtract,
  input  [31:0] in_34,
  input  [31:0] in_35,
  input  [31:0] in_36,
  input  [31:0] in_37,
  input  [31:0] randomGen,
  input  in_39,
  input  Reset,
  input  [31:0] in_41,
  input  [31:0] in_42,
  output out_43,
  output [31:0] out_44,
  output [31:0] out_45
);

  wire comparator_1_eq, comparator_2_eq, not_1_out, not_2_out, or_1_out;
  wire [3:0] adder_1_out, adder_2_out, counter_1_q, counter_2_q, multiplexer_2_out, multiplexer_3_out,
       register_2_q, register_3_q;
  wire [31:0] multiplexer_1_out, register_1_q;

  Register #(.width(32)) register_1 (.D(multiplexer_1_out), .Q(register_1_q), .clk(or_1_out));  // open: en, clr
  Multiplexer #(.width(32), .enable("false")) multiplexer_1 (
    .in0(out_44), .in1(randomGen), .out(multiplexer_1_out), .sel(Reset));
  or or_1 (or_1_out, Reset, in_39);
  Counter #(.width(4), .max('hf)) counter_1 (
    .Q(counter_1_q), .clk(in_12), .clr(comparator_1_eq));  // open: load, D, count, carry
  Comparator #(.width(4)) comparator_1 (.a(counter_1_q), .b(4'b1010), .eq(comparator_1_eq));  // open: gt, lt
  Subtractor #(.width(32)) subtractor_1 (.a(register_1_q), .b(gUpSubtract), .out(out_44));  // open: bin, bout
  assign out_45 = in_41 ^ in_42;  // XOR_Gate xor_1, 32 bits wide
  Hex_Digit_Display hex_digit_display_1 (.value(counter_2_q));  // open: dp
  Counter #(.width(4), .max('hf)) counter_2 (
    .Q(counter_2_q), .clk(comparator_1_eq));  // open: load, D, count, carry, clr
  Hex_Digit_Display hex_digit_display_2 (.value(counter_1_q));  // open: dp
  xor xor_2 (out_43, in_1, in_2, in_3, in_4, in_5);
  Multiplexer #(.width(4), .enable("false")) multiplexer_2 (
    .in0(4'b0000), .in1(4'b0001), .out(multiplexer_2_out), .sel(in_23));
  Multiplexer #(.width(4), .enable("false")) multiplexer_3 (
    .in0(4'b0000), .in1(4'b0001), .out(multiplexer_3_out), .sel(comparator_2_eq));
  Adder #(.width(4)) adder_1 (.a(register_2_q), .b(multiplexer_2_out), .out(adder_1_out));  // open: cin, cout
  not not_1 (not_1_out, in_23);
  Comparator #(.width(4)) comparator_2 (.a(register_2_q), .b(4'b1010), .eq(comparator_2_eq));  // open: gt, lt
  Adder #(.width(4)) adder_2 (.a(register_3_q), .b(multiplexer_3_out), .out(adder_2_out));  // open: cin, cout
  not not_2 (not_2_out, comparator_2_eq);
  Register #(.width(4)) register_2 (
    .D(adder_1_out), .Q(register_2_q), .clk(not_1_out), .clr(comparator_2_eq));  // open: en
  Register #(.width(4)) register_3 (.D(adder_2_out), .Q(register_3_q), .clk(not_2_out));  // open: en, clr
  Hex_Digit_Display hex_digit_display_3 (.value(register_3_q));  // open: dp
  Hex_Digit_Display hex_digit_display_4 (.value(register_2_q));  // open: dp
  DotMatrix #(.inputtype("row"), .matrixcols(32), .matrixrows(32)) dotmatrix_1 (
    .row0(in_6), .row1(in_7), .row2(in_9), .row3(in_14), .row4(in_19), .row5(in_25), .row6(in_30),
    .row7(in_36), .row8(in_8), .row9(in_11), .row10(in_16), .row11(in_21), .row12(in_27), .row13(in_32),
    .row14(in_10), .row15(in_15), .row16(in_20), .row17(in_26), .row18(in_31), .row19(in_37), .row20(in_13),
    .row21(in_18), .row22(in_24), .row23(in_29), .row24(in_35), .row25(in_17), .row26(in_22), .row27(in_28),
    .row28(in_34));  // open: row29, row30, row31

  // Notes on the sheet:
  //   in_13: pull=up
  //   in_15: pull=up
  //   in_20: pull=up
  //   in_25: pull=up
  //   in_17: pull=up
  //   in_9: pull=up
  //   in_16: pull=up
  //   in_21: pull=up
  //   in_24: pull=up
  //   in_35: pull=up
  //   in_11: pull=up
  //   in_14: pull=up
  //   in_36: pull=up
  //   in_32: pull=up
  //   in_10: pull=up
  //   in_19: pull=up
  //   in_7: pull=up
  //   in_30: pull=up
  //   in_6: pull=up
  //   in_34: pull=up
  //   in_8: pull=up
  //   in_29: pull=up
  //   in_18: pull=up
  //   in_27: pull=up
  //   in_26: pull=up
  //   in_28: pull=up
  //   in_31: pull=up
  //   in_37: pull=up
  //   in_22: pull=up
endmodule

module moveBullet (
  input  [31:0] Bullet,
  input  Tilt,
  input  Bounce,
  output [31:0] Moved_bullet,
  output Tilt_2,
  output Bounce_2
);

  wire comparator_1_eq, comparator_2_eq, comparator_3_eq, not_1_out, not_2_out;
  wire [1:0] and_2_out;
  wire [1:1] multiplexer_1_out;
  wire [31:0] shifter_1_out, shifter_2_out;

  not not_1 (not_1_out, Tilt);
  Comparator #(.width(32)) comparator_1 (.a(Bullet), .b(32'h80000000), .eq(comparator_1_eq));  // open: gt, lt
  not not_2 (not_2_out, not_1_out);
  Comparator #(.width(32)) comparator_2 (.a(Bullet), .b(32'h1), .eq(comparator_2_eq));  // open: gt, lt
  and and_1 (and_2_out[1], comparator_1_eq, not_2_out);
  and and_2 (and_2_out[0], comparator_2_eq, not_1_out);
  Shifter #(.width(32), .shift("lr")) shifter_1 (.in(Bullet), .\dist (5'b00001), .out(shifter_1_out));
  Shifter #(.width(32)) shifter_2 (.in(Bullet), .\dist (5'b00001), .out(shifter_2_out));
  Multiplexer #(.enable("false")) multiplexer_1 (
    .in0(Tilt), .in1(not_1_out), .out(multiplexer_1_out[1]), .sel(and_2_out[0]));
  Multiplexer #(.select(2), .enable("false")) multiplexer_2 (
    .in0(Bounce), .in1(1'b1), .in2(1'b1), .in3(Bounce), .out(Bounce_2), .sel(and_2_out));
  Multiplexer #(.select(2), .width(32), .enable("false")) multiplexer_3 (
    .in0(shifter_1_out), .in1(shifter_2_out), .in2(shifter_2_out), .in3(shifter_1_out), .out(Moved_bullet),
    .sel({multiplexer_1_out[1], and_2_out[1]}));
  Comparator #(.width(2)) comparator_3 (
    .a({multiplexer_1_out[1], and_2_out[1]}), .b(2'b11), .eq(comparator_3_eq));  // open: gt, lt
  Multiplexer #(.enable("false")) multiplexer_4 (
    .in0(multiplexer_1_out[1]), .in1(1'b0), .out(Tilt_2), .sel(comparator_3_eq));
endmodule

module rowReg (
  input  [31:0] Going_down_bullet,
  input  [31:0] Row_values,
  input  [31:0] Going_up_bullet,
  input  Tilt,
  input  Bounce,
  input  Tilt2,
  input  Bounce2,
  input  Clock,
  input  Reset,
  output [31:0] Going_down_bullet_2,
  output [31:0] Modified_row,
  output [31:0] Going_up_bullet_2,
  output Tilt_2,
  output Bounce_2,
  output Tilt2_2,
  output Bounce2_2,
  output [31:0] gUpSubtract,
  output [31:0] gDownSubtract,
  output downHit,
  output upHit
);

  wire rowcompare_1_hit, rowcompare_2_hit;
  wire [31:0] adder_1_out, register_3_q, rowcompare_1_bulletpos_2, rowcompare_1_rowvalue_2,
       rowcompare_2_bulletpos_2, rowcompare_2_rowvalue_2;

  D_Flip_Flop #(.trigger("falling")) d_ff_1 (
    .clk(Clock), .D(rowcompare_2_hit), .Q(downHit), .reset(Reset));  // open: Qn, preset, en
  rowCompare rowcompare_1 (
    .rowValue(Row_values), .bulletPos(Going_up_bullet), .Bounce(Bounce),
    .rowValue_2(rowcompare_1_rowvalue_2), .bulletPos_2(rowcompare_1_bulletpos_2), .Hit(rowcompare_1_hit));
  Register #(.width(32)) register_1 (
    .D(rowcompare_1_bulletpos_2), .Q(Going_up_bullet_2), .clk(Clock), .clr(Reset));  // open: en
  Register #(.width(32), .trigger("falling")) register_2 (
    .D(rowcompare_2_rowvalue_2), .Q(gDownSubtract), .clk(Clock), .clr(Reset));  // open: en
  Register #(.width(32)) register_3 (.D(Row_values), .Q(register_3_q), .clk(Clock), .clr(Reset));  // open: en
  D_Flip_Flop d_ff_2 (.clk(Clock), .D(Tilt), .Q(Tilt_2), .reset(Reset));  // open: Qn, preset, en
  D_Flip_Flop d_ff_3 (.clk(Clock), .D(Bounce), .Q(Bounce_2), .reset(Reset));  // open: Qn, preset, en
  D_Flip_Flop d_ff_4 (.clk(Clock), .D(Tilt2), .Q(Tilt2_2), .reset(Reset));  // open: Qn, preset, en
  D_Flip_Flop d_ff_5 (.clk(Clock), .D(Bounce2), .Q(Bounce2_2), .reset(Reset));  // open: Qn, preset, en
  Adder #(.width(32)) adder_1 (.a(Going_down_bullet_2), .b(register_3_q), .out(adder_1_out));  // open: cin, cout
  Register #(.width(32)) register_4 (
    .D(rowcompare_2_bulletpos_2), .Q(Going_down_bullet_2), .clk(Clock), .clr(Reset));  // open: en
  rowCompare rowcompare_2 (
    .rowValue(Row_values), .bulletPos(Going_down_bullet), .Bounce(Bounce2),
    .rowValue_2(rowcompare_2_rowvalue_2), .bulletPos_2(rowcompare_2_bulletpos_2), .Hit(rowcompare_2_hit));
  Adder #(.width(32)) adder_2 (.a(adder_1_out), .b(Going_up_bullet_2), .out(Modified_row));  // open: cin, cout
  Register #(.width(32), .trigger("falling")) register_5 (
    .D(rowcompare_1_rowvalue_2), .Q(gUpSubtract), .clk(Clock), .clr(Reset));  // open: en
  D_Flip_Flop #(.trigger("falling")) d_ff_6 (
    .clk(Clock), .D(rowcompare_1_hit), .Q(upHit), .reset(Reset));  // open: Qn, preset, en

  // Other names for the same wires on the sheet: B1 = Bounce; B2 = Bounce2
endmodule

module movement (
  input  [31:0] CannonPos,
  input  [31:0] BasePos,
  input  Fire,
  input  Tilt,
  input  Reset,
  input  Clock,
  output [3:0] score1,
  output [3:0] score0,
  output [31:0] out_9,
  output [31:0] out_10,
  output [31:0] out_11,
  output [31:0] out_12,
  output [31:0] out_13,
  output [31:0] out_14,
  output [31:0] out_15,
  output [31:0] out_16,
  output [31:0] out_17,
  output [31:0] out_18,
  output [31:0] out_19,
  output [31:0] out_20,
  output [31:0] out_21,
  output [31:0] out_22,
  output [31:0] out_23,
  output [31:0] out_24,
  output [31:0] out_25,
  output [31:0] out_26,
  output [31:0] out_27,
  output [31:0] out_28,
  output [31:0] out_29,
  output [31:0] out_30,
  output [31:0] out_31,
  output [31:0] out_32,
  output [31:0] out_33,
  output [31:0] out_34,
  output [31:0] out_35,
  output [31:0] out_36,
  output [31:0] out_37,
  output [31:0] out_38,
  output [31:0] out_39,
  output [31:0] out_40
);

  wire all0, and_1_out, cannonhit_1_out_5, comparator_1_eq, comparator_2_eq, comparator_3_eq,
       comparator_4_eq, comparator_5_eq, comparator_6_eq, comparator_7_eq, comparator_8_eq, comparator_9_eq,
       comparator_10_eq, comparator_11_eq, comparator_12_eq, comparator_13_eq, comparator_14_eq,
       comparator_15_eq, comparator_16_eq, comparator_17_eq, comparator_18_eq, comparator_19_eq,
       comparator_20_eq, comparator_21_eq, comparator_22_eq, comparator_23_eq, comparator_24_eq,
       comparator_25_eq, comparator_26_eq, comparator_27_eq, comparator_28_eq, comparator_29_eq,
       comparator_30_eq, comparator_31_eq, comparator_32_eq, h1, h2, h3, h4, h5, h6, h7, h8, h9, h10, lose,
       movebullet_1_bounce_2, movebullet_1_tilt_2, movebullet_2_bounce_2, movebullet_2_tilt_2,
       movebullet_3_bounce_2, movebullet_3_tilt_2, movebullet_4_bounce_2, movebullet_4_tilt_2,
       movebullet_5_bounce_2, movebullet_5_tilt_2, movebullet_6_bounce_2, movebullet_6_tilt_2,
       movebullet_7_bounce_2, movebullet_7_tilt_2, movebullet_8_bounce_2, movebullet_8_tilt_2,
       movebullet_9_bounce_2, movebullet_9_tilt_2, movebullet_10_bounce_2, movebullet_10_tilt_2,
       movebullet_11_bounce_2, movebullet_11_tilt_2, movebullet_12_bounce_2, movebullet_12_tilt_2,
       movebullet_13_bounce_2, movebullet_13_tilt_2, movebullet_14_bounce_2, movebullet_14_tilt_2,
       movebullet_15_bounce_2, movebullet_15_tilt_2, movebullet_16_bounce_2, movebullet_16_tilt_2,
       movebullet_17_bounce_2, movebullet_17_tilt_2, movebullet_18_bounce_2, movebullet_18_tilt_2,
       movebullet_19_bounce_2, movebullet_19_tilt_2, movebullet_20_bounce_2, movebullet_20_tilt_2,
       movebullet_21_bounce_2, movebullet_21_tilt_2, movebullet_22_bounce_2, movebullet_22_tilt_2,
       movebullet_23_bounce_2, movebullet_23_tilt_2, movebullet_24_bounce_2, movebullet_24_tilt_2,
       movebullet_25_bounce_2, movebullet_25_tilt_2, movebullet_26_bounce_2, movebullet_26_tilt_2,
       movebullet_27_bounce_2, movebullet_27_tilt_2, movebullet_28_bounce_2, movebullet_28_tilt_2,
       movebullet_29_bounce_2, movebullet_29_tilt_2, movebullet_30_bounce_2, movebullet_30_tilt_2,
       movebullet_31_bounce_2, movebullet_31_tilt_2, movebullet_32_bounce_2, movebullet_32_tilt_2,
       movebullet_33_bounce_2, movebullet_33_tilt_2, movebullet_34_bounce_2, movebullet_34_tilt_2,
       movebullet_35_bounce_2, movebullet_35_tilt_2, movebullet_36_bounce_2, movebullet_36_tilt_2,
       movebullet_37_bounce_2, movebullet_37_tilt_2, movebullet_38_bounce_2, movebullet_38_tilt_2,
       movebullet_39_bounce_2, movebullet_39_tilt_2, movebullet_40_bounce_2, movebullet_40_tilt_2,
       movebullet_41_bounce_2, movebullet_41_tilt_2, movebullet_42_bounce_2, movebullet_42_tilt_2,
       movebullet_43_bounce_2, movebullet_43_tilt_2, movebullet_44_bounce_2, movebullet_44_tilt_2,
       movebullet_45_bounce_2, movebullet_45_tilt_2, movebullet_46_bounce_2, movebullet_46_tilt_2,
       movebullet_47_bounce_2, movebullet_47_tilt_2, movebullet_48_bounce_2, movebullet_48_tilt_2,
       movebullet_49_bounce_2, movebullet_49_tilt_2, movebullet_50_bounce_2, movebullet_50_tilt_2,
       movebullet_51_bounce_2, movebullet_51_tilt_2, movebullet_52_bounce_2, movebullet_52_tilt_2,
       movebullet_53_bounce_2, movebullet_53_tilt_2, movebullet_54_bounce_2, movebullet_54_tilt_2,
       movebullet_55_bounce_2, movebullet_55_tilt_2, movebullet_56_bounce_2, movebullet_56_tilt_2,
       movebullet_57_bounce_2, movebullet_57_tilt_2, movebullet_58_bounce_2, movebullet_58_tilt_2,
       movebullet_59_bounce_2, movebullet_59_tilt_2, multiplexer_1_out, or_2_out, Reset_t, rowreg_1_bounce_2,
       rowreg_1_tilt2_2, rowreg_1_tilt_2, rowreg_2_bounce2_2, rowreg_2_bounce_2, rowreg_2_tilt2_2,
       rowreg_2_tilt_2, rowreg_3_bounce2_2, rowreg_3_bounce_2, rowreg_3_tilt2_2, rowreg_3_tilt_2,
       rowreg_4_bounce2_2, rowreg_4_bounce_2, rowreg_4_tilt2_2, rowreg_4_tilt_2, rowreg_5_bounce2_2,
       rowreg_5_bounce_2, rowreg_5_tilt2_2, rowreg_5_tilt_2, rowreg_6_bounce2_2, rowreg_6_bounce_2,
       rowreg_6_tilt2_2, rowreg_6_tilt_2, rowreg_7_bounce2_2, rowreg_7_bounce_2, rowreg_7_tilt2_2,
       rowreg_7_tilt_2, rowreg_8_bounce2_2, rowreg_8_bounce_2, rowreg_8_tilt2_2, rowreg_8_tilt_2,
       rowreg_9_bounce2_2, rowreg_9_bounce_2, rowreg_9_tilt2_2, rowreg_9_tilt_2, rowreg_10_bounce2_2,
       rowreg_10_bounce_2, rowreg_10_tilt2_2, rowreg_10_tilt_2, rowreg_11_bounce2_2, rowreg_11_bounce_2,
       rowreg_11_tilt2_2, rowreg_11_tilt_2, rowreg_12_bounce2_2, rowreg_12_bounce_2, rowreg_12_tilt2_2,
       rowreg_12_tilt_2, rowreg_13_bounce2_2, rowreg_13_bounce_2, rowreg_13_tilt2_2, rowreg_13_tilt_2,
       rowreg_14_bounce2_2, rowreg_14_bounce_2, rowreg_14_tilt2_2, rowreg_14_tilt_2, rowreg_15_bounce2_2,
       rowreg_15_bounce_2, rowreg_15_tilt2_2, rowreg_15_tilt_2, rowreg_16_bounce2_2, rowreg_16_bounce_2,
       rowreg_16_tilt2_2, rowreg_16_tilt_2, rowreg_17_bounce2_2, rowreg_17_bounce_2, rowreg_17_tilt2_2,
       rowreg_17_tilt_2, rowreg_18_bounce2_2, rowreg_18_bounce_2, rowreg_18_tilt2_2, rowreg_18_tilt_2,
       rowreg_19_bounce2_2, rowreg_19_bounce_2, rowreg_19_tilt2_2, rowreg_19_tilt_2, rowreg_20_bounce2_2,
       rowreg_20_bounce_2, rowreg_20_tilt2_2, rowreg_20_tilt_2, rowreg_21_bounce2_2, rowreg_21_bounce_2,
       rowreg_21_tilt2_2, rowreg_21_tilt_2, rowreg_22_bounce2_2, rowreg_22_bounce_2, rowreg_22_tilt2_2,
       rowreg_22_tilt_2, rowreg_23_bounce2_2, rowreg_23_bounce_2, rowreg_23_tilt2_2, rowreg_23_tilt_2,
       rowreg_24_bounce2_2, rowreg_24_bounce_2, rowreg_24_tilt2_2, rowreg_24_tilt_2, rowreg_25_bounce2_2,
       rowreg_25_bounce_2, rowreg_25_tilt2_2, rowreg_25_tilt_2, rowreg_26_bounce2_2, rowreg_26_bounce_2,
       rowreg_26_tilt2_2, rowreg_26_tilt_2, rowreg_27_bounce2_2, rowreg_27_bounce_2, rowreg_27_tilt2_2,
       rowreg_27_tilt_2, rowreg_28_bounce2_2, rowreg_28_bounce_2, rowreg_28_tilt2_2, rowreg_28_tilt_2,
       rowreg_29_bounce2_2, rowreg_29_bounce_2, rowreg_29_tilt2_2, rowreg_29_tilt_2, rowreg_30_bounce2_2,
       rowreg_30_bounce_2, rowreg_30_tilt2_2, rowreg_30_tilt_2;
  wire [29:0] random_5_out;
  wire [31:0] movebullet_1_moved_bullet, movebullet_2_moved_bullet, movebullet_3_moved_bullet,
       movebullet_4_moved_bullet, movebullet_5_moved_bullet, movebullet_6_moved_bullet,
       movebullet_7_moved_bullet, movebullet_8_moved_bullet, movebullet_9_moved_bullet,
       movebullet_10_moved_bullet, movebullet_11_moved_bullet, movebullet_12_moved_bullet,
       movebullet_13_moved_bullet, movebullet_14_moved_bullet, movebullet_15_moved_bullet,
       movebullet_16_moved_bullet, movebullet_17_moved_bullet, movebullet_18_moved_bullet,
       movebullet_19_moved_bullet, movebullet_20_moved_bullet, movebullet_21_moved_bullet,
       movebullet_22_moved_bullet, movebullet_23_moved_bullet, movebullet_24_moved_bullet,
       movebullet_25_moved_bullet, movebullet_26_moved_bullet, movebullet_27_moved_bullet,
       movebullet_28_moved_bullet, movebullet_29_moved_bullet, movebullet_30_moved_bullet,
       movebullet_31_moved_bullet, movebullet_32_moved_bullet, movebullet_33_moved_bullet,
       movebullet_34_moved_bullet, movebullet_35_moved_bullet, movebullet_36_moved_bullet,
       movebullet_37_moved_bullet, movebullet_38_moved_bullet, movebullet_39_moved_bullet,
       movebullet_40_moved_bullet, movebullet_41_moved_bullet, movebullet_42_moved_bullet,
       movebullet_43_moved_bullet, movebullet_44_moved_bullet, movebullet_45_moved_bullet,
       movebullet_46_moved_bullet, movebullet_47_moved_bullet, movebullet_48_moved_bullet,
       movebullet_49_moved_bullet, movebullet_50_moved_bullet, movebullet_51_moved_bullet,
       movebullet_52_moved_bullet, movebullet_53_moved_bullet, movebullet_54_moved_bullet,
       movebullet_55_moved_bullet, movebullet_56_moved_bullet, movebullet_57_moved_bullet,
       movebullet_58_moved_bullet, movebullet_59_moved_bullet, multiplexer_2_out, r0, r1, r2, r3, r4, r5, r6,
       r7, r8, r9, r10, r11, r12, r13, r14, r15, r16, r17, r18, r19, r20, r21, r22, r23, r24, r25, r26, r27,
       r28, r29, random_1_out, random_2_out, random_3_out, random_4_out, rowmodifier_1_out_7,
       rowmodifier_2_out_7, rowmodifier_3_out_7, rowmodifier_4_out_7, rowmodifier_5_out_7,
       rowreg_1_going_down_bullet_2, rowreg_1_going_up_bullet_2, rowreg_2_going_down_bullet_2,
       rowreg_2_going_up_bullet_2, rowreg_3_going_down_bullet_2, rowreg_3_going_up_bullet_2,
       rowreg_4_going_down_bullet_2, rowreg_4_going_up_bullet_2, rowreg_5_going_down_bullet_2,
       rowreg_5_going_up_bullet_2, rowreg_6_going_down_bullet_2, rowreg_6_going_up_bullet_2,
       rowreg_7_going_down_bullet_2, rowreg_7_going_up_bullet_2, rowreg_8_going_down_bullet_2,
       rowreg_8_going_up_bullet_2, rowreg_9_going_down_bullet_2, rowreg_9_going_up_bullet_2,
       rowreg_10_going_down_bullet_2, rowreg_10_going_up_bullet_2, rowreg_11_going_down_bullet_2,
       rowreg_11_going_up_bullet_2, rowreg_12_going_down_bullet_2, rowreg_12_going_up_bullet_2,
       rowreg_13_going_down_bullet_2, rowreg_13_going_up_bullet_2, rowreg_14_going_down_bullet_2,
       rowreg_14_going_up_bullet_2, rowreg_15_going_down_bullet_2, rowreg_15_going_up_bullet_2,
       rowreg_16_going_down_bullet_2, rowreg_16_going_up_bullet_2, rowreg_17_going_down_bullet_2,
       rowreg_17_going_up_bullet_2, rowreg_18_going_down_bullet_2, rowreg_18_going_up_bullet_2,
       rowreg_19_going_down_bullet_2, rowreg_19_going_up_bullet_2, rowreg_20_going_down_bullet_2,
       rowreg_20_going_up_bullet_2, rowreg_21_going_down_bullet_2, rowreg_21_going_up_bullet_2,
       rowreg_22_gdownsubtract, rowreg_22_going_down_bullet_2, rowreg_22_going_up_bullet_2,
       rowreg_22_gupsubtract, rowreg_23_going_down_bullet_2, rowreg_23_going_up_bullet_2,
       rowreg_24_gdownsubtract, rowreg_24_going_down_bullet_2, rowreg_24_going_up_bullet_2,
       rowreg_24_gupsubtract, rowreg_25_going_down_bullet_2, rowreg_25_going_up_bullet_2,
       rowreg_26_gdownsubtract, rowreg_26_going_down_bullet_2, rowreg_26_going_up_bullet_2,
       rowreg_26_gupsubtract, rowreg_27_going_down_bullet_2, rowreg_27_going_up_bullet_2,
       rowreg_28_gdownsubtract, rowreg_28_going_down_bullet_2, rowreg_28_going_up_bullet_2,
       rowreg_28_gupsubtract, rowreg_29_going_down_bullet_2, rowreg_29_going_up_bullet_2,
       rowreg_30_gdownsubtract, rowreg_30_going_down_bullet_2, rowreg_30_going_up_bullet_2,
       rowreg_30_gupsubtract;

  Multiplexer #(.enable("false")) multiplexer_1 (.in0(1'b0), .in1(Tilt), .out(multiplexer_1_out), .sel(Fire));
  Multiplexer #(.width(32), .enable("false")) multiplexer_2 (
    .in0({32{1'b0}}), .in1(CannonPos), .out(multiplexer_2_out), .sel(Fire));
  buf or_1 (Reset_t, Reset);  // OR_Gate
  Multiplexer #(.width(32), .enable("false")) multiplexer_3 (.in0(BasePos), .in1({32{1'b0}}), .out(out_40), .sel(all0));
  D_Flip_Flop d_ff_1 (.clk(cannonhit_1_out_5), .D(1'b1), .Q(lose), .reset(Reset_t));  // open: Qn, preset, en
  cannonHit cannonhit_1 (
    .cannonPos(CannonPos), .bulletPos(rowreg_1_going_down_bullet_2), .basePos(BasePos),
    .Tilt(rowreg_1_tilt2_2), .out_5(cannonhit_1_out_5));
  Comparator #(.width(32)) comparator_1 (
    .a(CannonPos), .b(rowreg_1_going_down_bullet_2), .eq(comparator_1_eq));  // open: gt, lt
  Multiplexer #(.width(32), .enable("false")) multiplexer_4 (
    .in0(CannonPos), .in1({32{1'b0}}), .out(out_39), .sel(all0));
  Comparator #(.width(32)) comparator_2 (
    .a(BasePos), .b(rowreg_1_going_down_bullet_2), .eq(comparator_2_eq));  // open: gt, lt
  rowReg rowreg_1 (
    .Going_down_bullet_2(rowreg_1_going_down_bullet_2), .Row_values({32{1'b0}}),
    .Going_up_bullet(multiplexer_2_out), .Tilt(multiplexer_1_out), .Bounce(1'b0), .Tilt2_2(rowreg_1_tilt2_2),
    .Clock(Clock), .Going_down_bullet(movebullet_1_moved_bullet), .Modified_row(r29),
    .Going_up_bullet_2(rowreg_1_going_up_bullet_2), .Tilt_2(rowreg_1_tilt_2), .Bounce_2(rowreg_1_bounce_2),
    .Tilt2(movebullet_1_tilt_2), .Bounce2(movebullet_1_bounce_2), .Reset(Reset_t));  // open: Bounce2_2, gDownSubtract, downHit, gUpSubtract, upHit
  moveBullet movebullet_1 (
    .Bullet(rowreg_2_going_down_bullet_2), .Tilt(rowreg_2_tilt2_2), .Bounce(rowreg_2_bounce2_2),
    .Moved_bullet(movebullet_1_moved_bullet), .Tilt_2(movebullet_1_tilt_2), .Bounce_2(movebullet_1_bounce_2));
  moveBullet movebullet_2 (
    .Bullet(rowreg_1_going_up_bullet_2), .Tilt(rowreg_1_tilt_2), .Bounce(rowreg_1_bounce_2),
    .Moved_bullet(movebullet_2_moved_bullet), .Tilt_2(movebullet_2_tilt_2), .Bounce_2(movebullet_2_bounce_2));
  Multiplexer #(.width(32), .enable("false")) multiplexer_5 (.in0(r29), .in1({32{1'b0}}), .out(out_38), .sel(all0));
  rowReg rowreg_2 (
    .Going_down_bullet_2(rowreg_2_going_down_bullet_2), .Row_values({32{1'b0}}),
    .Going_up_bullet(movebullet_2_moved_bullet), .Tilt(movebullet_2_tilt_2), .Bounce(movebullet_2_bounce_2),
    .Tilt2_2(rowreg_2_tilt2_2), .Bounce2_2(rowreg_2_bounce2_2), .Clock(Clock),
    .Going_down_bullet(movebullet_3_moved_bullet), .Modified_row(r28),
    .Going_up_bullet_2(rowreg_2_going_up_bullet_2), .Tilt_2(rowreg_2_tilt_2), .Bounce_2(rowreg_2_bounce_2),
    .Tilt2(movebullet_3_tilt_2), .Bounce2(movebullet_3_bounce_2), .Reset(Reset_t));  // open: gDownSubtract, downHit, gUpSubtract, upHit
  moveBullet movebullet_3 (
    .Bullet(rowreg_3_going_down_bullet_2), .Tilt(rowreg_3_tilt2_2), .Bounce(rowreg_3_bounce2_2),
    .Moved_bullet(movebullet_3_moved_bullet), .Tilt_2(movebullet_3_tilt_2), .Bounce_2(movebullet_3_bounce_2));
  Multiplexer #(.width(32), .enable("false")) multiplexer_6 (.in0(r28), .in1({32{1'b0}}), .out(out_37), .sel(all0));
  moveBullet movebullet_4 (
    .Bullet(rowreg_2_going_up_bullet_2), .Tilt(rowreg_2_tilt_2), .Bounce(rowreg_2_bounce_2),
    .Moved_bullet(movebullet_4_moved_bullet), .Tilt_2(movebullet_4_tilt_2), .Bounce_2(movebullet_4_bounce_2));
  rowReg rowreg_3 (
    .Going_down_bullet_2(rowreg_3_going_down_bullet_2), .Row_values({32{1'b0}}),
    .Going_up_bullet(movebullet_4_moved_bullet), .Tilt(movebullet_4_tilt_2), .Bounce(movebullet_4_bounce_2),
    .Tilt2_2(rowreg_3_tilt2_2), .Bounce2_2(rowreg_3_bounce2_2), .Clock(Clock),
    .Going_down_bullet(movebullet_5_moved_bullet), .Modified_row(r27),
    .Going_up_bullet_2(rowreg_3_going_up_bullet_2), .Tilt_2(rowreg_3_tilt_2), .Bounce_2(rowreg_3_bounce_2),
    .Tilt2(movebullet_5_tilt_2), .Bounce2(movebullet_5_bounce_2), .Reset(Reset_t));  // open: gDownSubtract, downHit, gUpSubtract, upHit
  Multiplexer #(.width(32), .enable("false")) multiplexer_7 (.in0(r27), .in1({32{1'b0}}), .out(out_36), .sel(all0));
  moveBullet movebullet_5 (
    .Bullet(rowreg_4_going_down_bullet_2), .Tilt(rowreg_4_tilt2_2), .Bounce(rowreg_4_bounce2_2),
    .Moved_bullet(movebullet_5_moved_bullet), .Tilt_2(movebullet_5_tilt_2), .Bounce_2(movebullet_5_bounce_2));
  moveBullet movebullet_6 (
    .Bullet(rowreg_3_going_up_bullet_2), .Tilt(rowreg_3_tilt_2), .Bounce(rowreg_3_bounce_2),
    .Moved_bullet(movebullet_6_moved_bullet), .Tilt_2(movebullet_6_tilt_2), .Bounce_2(movebullet_6_bounce_2));
  rowReg rowreg_4 (
    .Going_down_bullet_2(rowreg_4_going_down_bullet_2), .Row_values({32{1'b0}}),
    .Going_up_bullet(movebullet_6_moved_bullet), .Tilt(movebullet_6_tilt_2), .Bounce(movebullet_6_bounce_2),
    .Tilt2_2(rowreg_4_tilt2_2), .Bounce2_2(rowreg_4_bounce2_2), .Clock(Clock),
    .Going_down_bullet(movebullet_7_moved_bullet), .Modified_row(r26),
    .Going_up_bullet_2(rowreg_4_going_up_bullet_2), .Tilt_2(rowreg_4_tilt_2), .Bounce_2(rowreg_4_bounce_2),
    .Tilt2(movebullet_7_tilt_2), .Bounce2(movebullet_7_bounce_2), .Reset(Reset_t));  // open: gDownSubtract, downHit, gUpSubtract, upHit
  moveBullet movebullet_7 (
    .Bullet(rowreg_5_going_down_bullet_2), .Tilt(rowreg_5_tilt2_2), .Bounce(rowreg_5_bounce2_2),
    .Moved_bullet(movebullet_7_moved_bullet), .Tilt_2(movebullet_7_tilt_2), .Bounce_2(movebullet_7_bounce_2));
  moveBullet movebullet_8 (
    .Bullet(rowreg_4_going_up_bullet_2), .Tilt(rowreg_4_tilt_2), .Bounce(rowreg_4_bounce_2),
    .Moved_bullet(movebullet_8_moved_bullet), .Tilt_2(movebullet_8_tilt_2), .Bounce_2(movebullet_8_bounce_2));
  Multiplexer #(.width(32), .enable("false")) multiplexer_8 (.in0(r26), .in1({32{1'b0}}), .out(out_35), .sel(all0));
  rowReg rowreg_5 (
    .Going_down_bullet_2(rowreg_5_going_down_bullet_2), .Row_values({32{1'b0}}),
    .Going_up_bullet(movebullet_8_moved_bullet), .Tilt(movebullet_8_tilt_2), .Bounce(movebullet_8_bounce_2),
    .Tilt2_2(rowreg_5_tilt2_2), .Bounce2_2(rowreg_5_bounce2_2), .Clock(Clock),
    .Going_down_bullet(movebullet_9_moved_bullet), .Modified_row(r25),
    .Going_up_bullet_2(rowreg_5_going_up_bullet_2), .Tilt_2(rowreg_5_tilt_2), .Bounce_2(rowreg_5_bounce_2),
    .Tilt2(movebullet_9_tilt_2), .Bounce2(movebullet_9_bounce_2), .Reset(Reset_t));  // open: gDownSubtract, downHit, gUpSubtract, upHit
  moveBullet movebullet_9 (
    .Bullet(rowreg_6_going_down_bullet_2), .Tilt(rowreg_6_tilt2_2), .Bounce(rowreg_6_bounce2_2),
    .Moved_bullet(movebullet_9_moved_bullet), .Tilt_2(movebullet_9_tilt_2), .Bounce_2(movebullet_9_bounce_2));
  Multiplexer #(.width(32), .enable("false")) multiplexer_9 (.in0(r25), .in1({32{1'b0}}), .out(out_34), .sel(all0));
  moveBullet movebullet_10 (
    .Bullet(rowreg_5_going_up_bullet_2), .Tilt(rowreg_5_tilt_2), .Bounce(rowreg_5_bounce_2),
    .Moved_bullet(movebullet_10_moved_bullet), .Tilt_2(movebullet_10_tilt_2),
    .Bounce_2(movebullet_10_bounce_2));
  rowReg rowreg_6 (
    .Going_down_bullet_2(rowreg_6_going_down_bullet_2), .Row_values({32{1'b0}}),
    .Going_up_bullet(movebullet_10_moved_bullet), .Tilt(movebullet_10_tilt_2),
    .Bounce(movebullet_10_bounce_2), .Tilt2_2(rowreg_6_tilt2_2), .Bounce2_2(rowreg_6_bounce2_2),
    .Clock(Clock), .Going_down_bullet(movebullet_11_moved_bullet), .Modified_row(r24),
    .Going_up_bullet_2(rowreg_6_going_up_bullet_2), .Tilt_2(rowreg_6_tilt_2), .Bounce_2(rowreg_6_bounce_2),
    .Tilt2(movebullet_11_tilt_2), .Bounce2(movebullet_11_bounce_2), .Reset(Reset_t));  // open: gDownSubtract, downHit, gUpSubtract, upHit
  Multiplexer #(.width(32), .enable("false")) multiplexer_10 (.in0(r24), .in1({32{1'b0}}), .out(out_33), .sel(all0));
  moveBullet movebullet_11 (
    .Bullet(rowreg_7_going_down_bullet_2), .Tilt(rowreg_7_tilt2_2), .Bounce(rowreg_7_bounce2_2),
    .Moved_bullet(movebullet_11_moved_bullet), .Tilt_2(movebullet_11_tilt_2),
    .Bounce_2(movebullet_11_bounce_2));
  moveBullet movebullet_12 (
    .Bullet(rowreg_6_going_up_bullet_2), .Tilt(rowreg_6_tilt_2), .Bounce(rowreg_6_bounce_2),
    .Moved_bullet(movebullet_12_moved_bullet), .Tilt_2(movebullet_12_tilt_2),
    .Bounce_2(movebullet_12_bounce_2));
  rowReg rowreg_7 (
    .Going_down_bullet_2(rowreg_7_going_down_bullet_2), .Row_values({32{1'b0}}),
    .Going_up_bullet(movebullet_12_moved_bullet), .Tilt(movebullet_12_tilt_2),
    .Bounce(movebullet_12_bounce_2), .Tilt2_2(rowreg_7_tilt2_2), .Bounce2_2(rowreg_7_bounce2_2),
    .Clock(Clock), .Going_down_bullet(movebullet_13_moved_bullet), .Modified_row(r23),
    .Going_up_bullet_2(rowreg_7_going_up_bullet_2), .Tilt_2(rowreg_7_tilt_2), .Bounce_2(rowreg_7_bounce_2),
    .Tilt2(movebullet_13_tilt_2), .Bounce2(movebullet_13_bounce_2), .Reset(Reset_t));  // open: gDownSubtract, downHit, gUpSubtract, upHit
  moveBullet movebullet_13 (
    .Bullet(rowreg_8_going_down_bullet_2), .Tilt(rowreg_8_tilt2_2), .Bounce(rowreg_8_bounce2_2),
    .Moved_bullet(movebullet_13_moved_bullet), .Tilt_2(movebullet_13_tilt_2),
    .Bounce_2(movebullet_13_bounce_2));
  Multiplexer #(.width(32), .enable("false")) multiplexer_11 (.in0(r23), .in1(32'he10f908), .out(out_32), .sel(all0));
  moveBullet movebullet_14 (
    .Bullet(rowreg_7_going_up_bullet_2), .Tilt(rowreg_7_tilt_2), .Bounce(rowreg_7_bounce_2),
    .Moved_bullet(movebullet_14_moved_bullet), .Tilt_2(movebullet_14_tilt_2),
    .Bounce_2(movebullet_14_bounce_2));
  rowReg rowreg_8 (
    .Going_down_bullet_2(rowreg_8_going_down_bullet_2), .Row_values({32{1'b0}}),
    .Going_up_bullet(movebullet_14_moved_bullet), .Tilt(movebullet_14_tilt_2),
    .Bounce(movebullet_14_bounce_2), .Tilt2_2(rowreg_8_tilt2_2), .Bounce2_2(rowreg_8_bounce2_2),
    .Clock(Clock), .Going_down_bullet(movebullet_15_moved_bullet), .Modified_row(r22),
    .Going_up_bullet_2(rowreg_8_going_up_bullet_2), .Tilt_2(rowreg_8_tilt_2), .Bounce_2(rowreg_8_bounce_2),
    .Tilt2(movebullet_15_tilt_2), .Bounce2(movebullet_15_bounce_2), .Reset(Reset_t));  // open: gDownSubtract, downHit, gUpSubtract, upHit
  Multiplexer #(.width(32), .enable("false")) multiplexer_12 (.in0(r22), .in1(32'h11290108), .out(out_31), .sel(all0));
  moveBullet movebullet_15 (
    .Bullet(rowreg_9_going_down_bullet_2), .Tilt(rowreg_9_tilt2_2), .Bounce(rowreg_9_bounce2_2),
    .Moved_bullet(movebullet_15_moved_bullet), .Tilt_2(movebullet_15_tilt_2),
    .Bounce_2(movebullet_15_bounce_2));
  moveBullet movebullet_16 (
    .Bullet(rowreg_8_going_up_bullet_2), .Tilt(rowreg_8_tilt_2), .Bounce(rowreg_8_bounce_2),
    .Moved_bullet(movebullet_16_moved_bullet), .Tilt_2(movebullet_16_tilt_2),
    .Bounce_2(movebullet_16_bounce_2));
  rowReg rowreg_9 (
    .Going_down_bullet_2(rowreg_9_going_down_bullet_2), .Row_values({32{1'b0}}),
    .Going_up_bullet(movebullet_16_moved_bullet), .Tilt(movebullet_16_tilt_2),
    .Bounce(movebullet_16_bounce_2), .Tilt2_2(rowreg_9_tilt2_2), .Bounce2_2(rowreg_9_bounce2_2),
    .Clock(Clock), .Going_down_bullet(movebullet_17_moved_bullet), .Modified_row(r21),
    .Going_up_bullet_2(rowreg_9_going_up_bullet_2), .Tilt_2(rowreg_9_tilt_2), .Bounce_2(rowreg_9_bounce_2),
    .Tilt2(movebullet_17_tilt_2), .Bounce2(movebullet_17_bounce_2), .Reset(Reset_t));  // open: gDownSubtract, downHit, gUpSubtract, upHit
  moveBullet movebullet_17 (
    .Bullet(rowreg_10_going_down_bullet_2), .Tilt(rowreg_10_tilt2_2), .Bounce(rowreg_10_bounce2_2),
    .Moved_bullet(movebullet_17_moved_bullet), .Tilt_2(movebullet_17_tilt_2),
    .Bounce_2(movebullet_17_bounce_2));
  moveBullet movebullet_18 (
    .Bullet(rowreg_9_going_up_bullet_2), .Tilt(rowreg_9_tilt_2), .Bounce(rowreg_9_bounce_2),
    .Moved_bullet(movebullet_18_moved_bullet), .Tilt_2(movebullet_18_tilt_2),
    .Bounce_2(movebullet_18_bounce_2));
  Multiplexer #(.width(32), .enable("false")) multiplexer_13 (.in0(r21), .in1(32'h11450108), .out(out_30), .sel(all0));
  rowReg rowreg_10 (
    .Going_down_bullet_2(rowreg_10_going_down_bullet_2), .Row_values({32{1'b0}}),
    .Going_up_bullet(movebullet_18_moved_bullet), .Tilt(movebullet_18_tilt_2),
    .Bounce(movebullet_18_bounce_2), .Tilt2_2(rowreg_10_tilt2_2), .Bounce2_2(rowreg_10_bounce2_2),
    .Clock(Clock), .Going_down_bullet(movebullet_19_moved_bullet), .Modified_row(r20),
    .Going_up_bullet_2(rowreg_10_going_up_bullet_2), .Tilt_2(rowreg_10_tilt_2),
    .Bounce_2(rowreg_10_bounce_2), .Tilt2(movebullet_19_tilt_2), .Bounce2(movebullet_19_bounce_2),
    .Reset(Reset_t));  // open: gDownSubtract, downHit, gUpSubtract, upHit
  moveBullet movebullet_19 (
    .Bullet(rowreg_11_going_down_bullet_2), .Tilt(rowreg_11_tilt2_2), .Bounce(rowreg_11_bounce2_2),
    .Moved_bullet(movebullet_19_moved_bullet), .Tilt_2(movebullet_19_tilt_2),
    .Bounce_2(movebullet_19_bounce_2));
  Multiplexer #(.width(32), .enable("false")) multiplexer_14 (.in0(r20), .in1(32'h1145f1f0), .out(out_29), .sel(all0));
  moveBullet movebullet_20 (
    .Bullet(rowreg_10_going_up_bullet_2), .Tilt(rowreg_10_tilt_2), .Bounce(rowreg_10_bounce_2),
    .Moved_bullet(movebullet_20_moved_bullet), .Tilt_2(movebullet_20_tilt_2),
    .Bounce_2(movebullet_20_bounce_2));
  rowReg rowreg_11 (
    .Going_down_bullet_2(rowreg_11_going_down_bullet_2), .Row_values({32{1'b0}}),
    .Going_up_bullet(movebullet_20_moved_bullet), .Tilt(movebullet_20_tilt_2),
    .Bounce(movebullet_20_bounce_2), .Tilt2_2(rowreg_11_tilt2_2), .Bounce2_2(rowreg_11_bounce2_2),
    .Clock(Clock), .Going_down_bullet(movebullet_21_moved_bullet), .Modified_row(r19),
    .Going_up_bullet_2(rowreg_11_going_up_bullet_2), .Tilt_2(rowreg_11_tilt_2),
    .Bounce_2(rowreg_11_bounce_2), .Tilt2(movebullet_21_tilt_2), .Bounce2(movebullet_21_bounce_2),
    .Reset(Reset_t));  // open: gDownSubtract, downHit, gUpSubtract, upHit
  Multiplexer #(.width(32), .enable("false")) multiplexer_15 (.in0(r19), .in1(32'h11450108), .out(out_28), .sel(all0));
  moveBullet movebullet_21 (
    .Bullet(rowreg_12_going_down_bullet_2), .Tilt(rowreg_12_tilt2_2), .Bounce(rowreg_12_bounce2_2),
    .Moved_bullet(movebullet_21_moved_bullet), .Tilt_2(movebullet_21_tilt_2),
    .Bounce_2(movebullet_21_bounce_2));
  moveBullet movebullet_22 (
    .Bullet(rowreg_11_going_up_bullet_2), .Tilt(rowreg_11_tilt_2), .Bounce(rowreg_11_bounce_2),
    .Moved_bullet(movebullet_22_moved_bullet), .Tilt_2(movebullet_22_tilt_2),
    .Bounce_2(movebullet_22_bounce_2));
  rowReg rowreg_12 (
    .Going_down_bullet_2(rowreg_12_going_down_bullet_2), .Row_values({32{1'b0}}),
    .Going_up_bullet(movebullet_22_moved_bullet), .Tilt(movebullet_22_tilt_2),
    .Bounce(movebullet_22_bounce_2), .Tilt2_2(rowreg_12_tilt2_2), .Bounce2_2(rowreg_12_bounce2_2),
    .Clock(Clock), .Going_down_bullet(movebullet_23_moved_bullet), .Modified_row(r18),
    .Going_up_bullet_2(rowreg_12_going_up_bullet_2), .Tilt_2(rowreg_12_tilt_2),
    .Bounce_2(rowreg_12_bounce_2), .Tilt2(movebullet_23_tilt_2), .Bounce2(movebullet_23_bounce_2),
    .Reset(Reset_t));  // open: gDownSubtract, downHit, gUpSubtract, upHit
  moveBullet movebullet_23 (
    .Bullet(rowreg_13_going_down_bullet_2), .Tilt(rowreg_13_tilt2_2), .Bounce(rowreg_13_bounce2_2),
    .Moved_bullet(movebullet_23_moved_bullet), .Tilt_2(movebullet_23_tilt_2),
    .Bounce_2(movebullet_23_bounce_2));
  moveBullet movebullet_24 (
    .Bullet(rowreg_12_going_up_bullet_2), .Tilt(rowreg_12_tilt_2), .Bounce(rowreg_12_bounce_2),
    .Moved_bullet(movebullet_24_moved_bullet), .Tilt_2(movebullet_24_tilt_2),
    .Bounce_2(movebullet_24_bounce_2));
  Multiplexer #(.width(32), .enable("false")) multiplexer_16 (.in0(r18), .in1(32'h11450108), .out(out_27), .sel(all0));
  rowReg rowreg_13 (
    .Going_down_bullet_2(rowreg_13_going_down_bullet_2), .Row_values({32{1'b0}}),
    .Going_up_bullet(movebullet_24_moved_bullet), .Tilt(movebullet_24_tilt_2),
    .Bounce(movebullet_24_bounce_2), .Tilt2_2(rowreg_13_tilt2_2), .Bounce2_2(rowreg_13_bounce2_2),
    .Clock(Clock), .Going_down_bullet(movebullet_25_moved_bullet), .Modified_row(r17),
    .Going_up_bullet_2(rowreg_13_going_up_bullet_2), .Tilt_2(rowreg_13_tilt_2),
    .Bounce_2(rowreg_13_bounce_2), .Tilt2(movebullet_25_tilt_2), .Bounce2(movebullet_25_bounce_2),
    .Reset(Reset_t));  // open: gDownSubtract, downHit, gUpSubtract, upHit
  moveBullet movebullet_25 (
    .Bullet(rowreg_14_going_down_bullet_2), .Tilt(rowreg_14_tilt2_2), .Bounce(rowreg_14_bounce2_2),
    .Moved_bullet(movebullet_25_moved_bullet), .Tilt_2(movebullet_25_tilt_2),
    .Bounce_2(movebullet_25_bounce_2));
  Multiplexer #(.width(32), .enable("false")) multiplexer_17 (.in0(r17), .in1(32'he44f9f0), .out(out_26), .sel(all0));
  moveBullet movebullet_26 (
    .Bullet(rowreg_13_going_up_bullet_2), .Tilt(rowreg_13_tilt_2), .Bounce(rowreg_13_bounce_2),
    .Moved_bullet(movebullet_26_moved_bullet), .Tilt_2(movebullet_26_tilt_2),
    .Bounce_2(movebullet_26_bounce_2));
  rowReg rowreg_14 (
    .Going_down_bullet_2(rowreg_14_going_down_bullet_2), .Row_values({32{1'b0}}),
    .Going_up_bullet(movebullet_26_moved_bullet), .Tilt(movebullet_26_tilt_2),
    .Bounce(movebullet_26_bounce_2), .Tilt2_2(rowreg_14_tilt2_2), .Bounce2_2(rowreg_14_bounce2_2),
    .Clock(Clock), .Going_down_bullet(movebullet_27_moved_bullet), .Modified_row(r16),
    .Going_up_bullet_2(rowreg_14_going_up_bullet_2), .Tilt_2(rowreg_14_tilt_2),
    .Bounce_2(rowreg_14_bounce_2), .Tilt2(movebullet_27_tilt_2), .Bounce2(movebullet_27_bounce_2),
    .Reset(Reset_t));  // open: gDownSubtract, downHit, gUpSubtract, upHit
  Multiplexer #(.width(32), .enable("false")) multiplexer_18 (.in0(r16), .in1({32{1'b0}}), .out(out_25), .sel(all0));
  moveBullet movebullet_27 (
    .Bullet(rowreg_15_going_down_bullet_2), .Tilt(rowreg_15_tilt2_2), .Bounce(rowreg_15_bounce2_2),
    .Moved_bullet(movebullet_27_moved_bullet), .Tilt_2(movebullet_27_tilt_2),
    .Bounce_2(movebullet_27_bounce_2));
  moveBullet movebullet_28 (
    .Bullet(rowreg_14_going_up_bullet_2), .Tilt(rowreg_14_tilt_2), .Bounce(rowreg_14_bounce_2),
    .Moved_bullet(movebullet_28_moved_bullet), .Tilt_2(movebullet_28_tilt_2),
    .Bounce_2(movebullet_28_bounce_2));
  rowReg rowreg_15 (
    .Going_down_bullet_2(rowreg_15_going_down_bullet_2), .Row_values({32{1'b0}}),
    .Going_up_bullet(movebullet_28_moved_bullet), .Tilt(movebullet_28_tilt_2),
    .Bounce(movebullet_28_bounce_2), .Tilt2_2(rowreg_15_tilt2_2), .Bounce2_2(rowreg_15_bounce2_2),
    .Clock(Clock), .Going_down_bullet(movebullet_29_moved_bullet), .Modified_row(r15),
    .Going_up_bullet_2(rowreg_15_going_up_bullet_2), .Tilt_2(rowreg_15_tilt_2),
    .Bounce_2(rowreg_15_bounce_2), .Tilt2(movebullet_29_tilt_2), .Bounce2(movebullet_29_bounce_2),
    .Reset(Reset_t));  // open: gDownSubtract, downHit, gUpSubtract, upHit
  moveBullet movebullet_29 (
    .Bullet(rowreg_16_going_down_bullet_2), .Tilt(rowreg_16_tilt2_2), .Bounce(rowreg_16_bounce2_2),
    .Moved_bullet(movebullet_29_moved_bullet), .Tilt_2(movebullet_29_tilt_2),
    .Bounce_2(movebullet_29_bounce_2));
  Multiplexer #(.width(32), .enable("false")) multiplexer_19 (.in0(r15), .in1({32{1'b0}}), .out(out_24), .sel(all0));
  moveBullet movebullet_30 (
    .Bullet(rowreg_15_going_up_bullet_2), .Tilt(rowreg_15_tilt_2), .Bounce(rowreg_15_bounce_2),
    .Moved_bullet(movebullet_30_moved_bullet), .Tilt_2(movebullet_30_tilt_2),
    .Bounce_2(movebullet_30_bounce_2));
  rowReg rowreg_16 (
    .Going_down_bullet_2(rowreg_16_going_down_bullet_2), .Row_values({32{1'b0}}),
    .Going_up_bullet(movebullet_30_moved_bullet), .Tilt(movebullet_30_tilt_2),
    .Bounce(movebullet_30_bounce_2), .Tilt2_2(rowreg_16_tilt2_2), .Bounce2_2(rowreg_16_bounce2_2),
    .Clock(Clock), .Going_down_bullet(movebullet_31_moved_bullet), .Modified_row(r14),
    .Going_up_bullet_2(rowreg_16_going_up_bullet_2), .Tilt_2(rowreg_16_tilt_2),
    .Bounce_2(rowreg_16_bounce_2), .Tilt2(movebullet_31_tilt_2), .Bounce2(movebullet_31_bounce_2),
    .Reset(Reset_t));  // open: gDownSubtract, downHit, gUpSubtract, upHit
  Multiplexer #(.width(32), .enable("false")) multiplexer_20 (.in0(r14), .in1(32'he4524f8), .out(out_23), .sel(all0));
  moveBullet movebullet_31 (
    .Bullet(rowreg_17_going_down_bullet_2), .Tilt(rowreg_17_tilt2_2), .Bounce(rowreg_17_bounce2_2),
    .Moved_bullet(movebullet_31_moved_bullet), .Tilt_2(movebullet_31_tilt_2),
    .Bounce_2(movebullet_31_bounce_2));
  moveBullet movebullet_32 (
    .Bullet(rowreg_16_going_up_bullet_2), .Tilt(rowreg_16_tilt_2), .Bounce(rowreg_16_bounce_2),
    .Moved_bullet(movebullet_32_moved_bullet), .Tilt_2(movebullet_32_tilt_2),
    .Bounce_2(movebullet_32_bounce_2));
  rowReg rowreg_17 (
    .Going_down_bullet_2(rowreg_17_going_down_bullet_2), .Row_values({32{1'b0}}),
    .Going_up_bullet(movebullet_32_moved_bullet), .Tilt(movebullet_32_tilt_2),
    .Bounce(movebullet_32_bounce_2), .Tilt2_2(rowreg_17_tilt2_2), .Bounce2_2(rowreg_17_bounce2_2),
    .Clock(Clock), .Going_down_bullet(movebullet_33_moved_bullet), .Modified_row(r13),
    .Going_up_bullet_2(rowreg_17_going_up_bullet_2), .Tilt_2(rowreg_17_tilt_2),
    .Bounce_2(rowreg_17_bounce_2), .Tilt2(movebullet_33_tilt_2), .Bounce2(movebullet_33_bounce_2),
    .Reset(Reset_t));  // open: gDownSubtract, downHit, gUpSubtract, upHit
  moveBullet movebullet_33 (
    .Bullet(rowreg_18_going_down_bullet_2), .Tilt(rowreg_18_tilt2_2), .Bounce(rowreg_18_bounce2_2),
    .Moved_bullet(movebullet_33_moved_bullet), .Tilt_2(movebullet_33_tilt_2),
    .Bounce_2(movebullet_33_bounce_2));
  moveBullet movebullet_34 (
    .Bullet(rowreg_17_going_up_bullet_2), .Tilt(rowreg_17_tilt_2), .Bounce(rowreg_17_bounce_2),
    .Moved_bullet(movebullet_34_moved_bullet), .Tilt_2(movebullet_34_tilt_2),
    .Bounce_2(movebullet_34_bounce_2));
  Multiplexer #(.width(32), .enable("false")) multiplexer_21 (.in0(r13), .in1(32'h11452500), .out(out_22), .sel(all0));
  rowReg rowreg_18 (
    .Going_down_bullet_2(rowreg_18_going_down_bullet_2), .Row_values({32{1'b0}}),
    .Going_up_bullet(movebullet_34_moved_bullet), .Tilt(movebullet_34_tilt_2),
    .Bounce(movebullet_34_bounce_2), .Tilt2_2(rowreg_18_tilt2_2), .Bounce2_2(rowreg_18_bounce2_2),
    .Clock(Clock), .Going_down_bullet(movebullet_35_moved_bullet), .Modified_row(r12),
    .Going_up_bullet_2(rowreg_18_going_up_bullet_2), .Tilt_2(rowreg_18_tilt_2),
    .Bounce_2(rowreg_18_bounce_2), .Tilt2(movebullet_35_tilt_2), .Bounce2(movebullet_35_bounce_2),
    .Reset(Reset_t));  // open: gDownSubtract, downHit, gUpSubtract, upHit
  moveBullet movebullet_35 (
    .Bullet(rowreg_19_going_down_bullet_2), .Tilt(rowreg_19_tilt2_2), .Bounce(rowreg_19_bounce2_2),
    .Moved_bullet(movebullet_35_moved_bullet), .Tilt_2(movebullet_35_tilt_2),
    .Bounce_2(movebullet_35_bounce_2));
  Multiplexer #(.width(32), .enable("false")) multiplexer_22 (.in0(r12), .in1(32'h117d2500), .out(out_21), .sel(all0));
  moveBullet movebullet_36 (
    .Bullet(rowreg_18_going_up_bullet_2), .Tilt(rowreg_18_tilt_2), .Bounce(rowreg_18_bounce_2),
    .Moved_bullet(movebullet_36_moved_bullet), .Tilt_2(movebullet_36_tilt_2),
    .Bounce_2(movebullet_36_bounce_2));
  rowReg rowreg_19 (
    .Going_down_bullet_2(rowreg_19_going_down_bullet_2), .Row_values({32{1'b0}}),
    .Going_up_bullet(movebullet_36_moved_bullet), .Tilt(movebullet_36_tilt_2),
    .Bounce(movebullet_36_bounce_2), .Tilt2_2(rowreg_19_tilt2_2), .Bounce2_2(rowreg_19_bounce2_2),
    .Clock(Clock), .Going_down_bullet(movebullet_37_moved_bullet), .Modified_row(r11),
    .Going_up_bullet_2(rowreg_19_going_up_bullet_2), .Tilt_2(rowreg_19_tilt_2),
    .Bounce_2(rowreg_19_bounce_2), .Tilt2(movebullet_37_tilt_2), .Bounce2(movebullet_37_bounce_2),
    .Reset(Reset_t));  // open: gDownSubtract, downHit, gUpSubtract, upHit
  Multiplexer #(.width(32), .enable("false")) multiplexer_23 (.in0(r11), .in1(32'h174525f0), .out(out_20), .sel(all0));
  moveBullet movebullet_37 (
    .Bullet(rowreg_20_going_down_bullet_2), .Tilt(rowreg_20_tilt2_2), .Bounce(rowreg_20_bounce2_2),
    .Moved_bullet(movebullet_37_moved_bullet), .Tilt_2(movebullet_37_tilt_2),
    .Bounce_2(movebullet_37_bounce_2));
  moveBullet movebullet_38 (
    .Bullet(rowreg_19_going_up_bullet_2), .Tilt(rowreg_19_tilt_2), .Bounce(rowreg_19_bounce_2),
    .Moved_bullet(movebullet_38_moved_bullet), .Tilt_2(movebullet_38_tilt_2),
    .Bounce_2(movebullet_38_bounce_2));
  rowReg rowreg_20 (
    .Going_down_bullet_2(rowreg_20_going_down_bullet_2), .Row_values({32{1'b0}}),
    .Going_up_bullet(movebullet_38_moved_bullet), .Tilt(movebullet_38_tilt_2),
    .Bounce(movebullet_38_bounce_2), .Tilt2_2(rowreg_20_tilt2_2), .Bounce2_2(rowreg_20_bounce2_2),
    .Clock(Clock), .Going_down_bullet(movebullet_39_moved_bullet), .Modified_row(r10),
    .Going_up_bullet_2(rowreg_20_going_up_bullet_2), .Tilt_2(rowreg_20_tilt_2),
    .Bounce_2(rowreg_20_bounce_2), .Tilt2(movebullet_39_tilt_2), .Bounce2(movebullet_39_bounce_2),
    .Reset(Reset_t));  // open: gDownSubtract, downHit, gUpSubtract, upHit
  moveBullet movebullet_39 (
    .Bullet(rowreg_21_going_down_bullet_2), .Tilt(rowreg_21_tilt2_2), .Bounce(rowreg_21_bounce2_2),
    .Moved_bullet(movebullet_39_moved_bullet), .Tilt_2(movebullet_39_tilt_2),
    .Bounce_2(movebullet_39_bounce_2));
  moveBullet movebullet_40 (
    .Bullet(rowreg_20_going_up_bullet_2), .Tilt(rowreg_20_tilt_2), .Bounce(rowreg_20_bounce_2),
    .Moved_bullet(movebullet_40_moved_bullet), .Tilt_2(movebullet_40_tilt_2),
    .Bounce_2(movebullet_40_bounce_2));
  Multiplexer #(.width(32), .enable("false")) multiplexer_24 (.in0(r10), .in1(32'h10452500), .out(out_19), .sel(all0));
  rowReg rowreg_21 (
    .Going_down_bullet_2(rowreg_21_going_down_bullet_2), .Row_values({32{1'b0}}),
    .Going_up_bullet(movebullet_40_moved_bullet), .Tilt(movebullet_40_tilt_2),
    .Bounce(movebullet_40_bounce_2), .Tilt2_2(rowreg_21_tilt2_2), .Bounce2_2(rowreg_21_bounce2_2),
    .Clock(Clock), .Going_down_bullet(movebullet_41_moved_bullet), .Modified_row(r9),
    .Going_up_bullet_2(rowreg_21_going_up_bullet_2), .Tilt_2(rowreg_21_tilt_2),
    .Bounce_2(rowreg_21_bounce_2), .Tilt2(movebullet_41_tilt_2), .Bounce2(movebullet_41_bounce_2),
    .Reset(Reset_t));  // open: gDownSubtract, downHit, gUpSubtract, upHit
  Random #(.width(32), .seed(113)) random_1 (.clk(Reset_t), .out(random_1_out));  // open: next, clr
  moveBullet movebullet_41 (
    .Bullet(rowreg_22_going_down_bullet_2), .Tilt(rowreg_22_tilt2_2), .Bounce(rowreg_22_bounce2_2),
    .Moved_bullet(movebullet_41_moved_bullet), .Tilt_2(movebullet_41_tilt_2),
    .Bounce_2(movebullet_41_bounce_2));
  Multiplexer #(.width(32), .enable("false")) multiplexer_25 (.in0(r9), .in1(32'h10295500), .out(out_18), .sel(all0));
  rowModifier rowmodifier_1 (
    .randomGen(random_1_out), .Reset(Reset_t), .gDownSubtract(rowreg_22_gdownsubtract), .downHit(h1),
    .gUpSubtract(rowreg_22_gupsubtract), .upHit(h2), .out_7(rowmodifier_1_out_7));
  moveBullet movebullet_42 (
    .Bullet(rowreg_21_going_up_bullet_2), .Tilt(rowreg_21_tilt_2), .Bounce(rowreg_21_bounce_2),
    .Moved_bullet(movebullet_42_moved_bullet), .Tilt_2(movebullet_42_tilt_2),
    .Bounce_2(movebullet_42_bounce_2));
  rowReg rowreg_22 (
    .Going_down_bullet_2(rowreg_22_going_down_bullet_2), .Row_values(rowmodifier_1_out_7),
    .Going_up_bullet(movebullet_42_moved_bullet), .Tilt(movebullet_42_tilt_2),
    .Bounce(movebullet_42_bounce_2), .Tilt2_2(rowreg_22_tilt2_2), .Bounce2_2(rowreg_22_bounce2_2),
    .gDownSubtract(rowreg_22_gdownsubtract), .downHit(h1), .Clock(Clock),
    .Going_down_bullet(movebullet_43_moved_bullet), .Modified_row(r8),
    .Going_up_bullet_2(rowreg_22_going_up_bullet_2), .Tilt_2(rowreg_22_tilt_2),
    .Bounce_2(rowreg_22_bounce_2), .Tilt2(movebullet_43_tilt_2), .Bounce2(movebullet_43_bounce_2),
    .gUpSubtract(rowreg_22_gupsubtract), .upHit(h2), .Reset(Reset_t));
  Multiplexer #(.width(32), .enable("false")) multiplexer_26 (.in0(r8), .in1(32'he1088f8), .out(out_17), .sel(all0));
  moveBullet movebullet_43 (
    .Bullet(rowreg_23_going_down_bullet_2), .Tilt(rowreg_23_tilt2_2), .Bounce(rowreg_23_bounce2_2),
    .Moved_bullet(movebullet_43_moved_bullet), .Tilt_2(movebullet_43_tilt_2),
    .Bounce_2(movebullet_43_bounce_2));
  moveBullet movebullet_44 (
    .Bullet(rowreg_22_going_up_bullet_2), .Tilt(rowreg_22_tilt_2), .Bounce(rowreg_22_bounce_2),
    .Moved_bullet(movebullet_44_moved_bullet), .Tilt_2(movebullet_44_tilt_2),
    .Bounce_2(movebullet_44_bounce_2));
  rowReg rowreg_23 (
    .Going_down_bullet_2(rowreg_23_going_down_bullet_2), .Row_values({32{1'b0}}),
    .Going_up_bullet(movebullet_44_moved_bullet), .Tilt(movebullet_44_tilt_2),
    .Bounce(movebullet_44_bounce_2), .Tilt2_2(rowreg_23_tilt2_2), .Bounce2_2(rowreg_23_bounce2_2),
    .Clock(Clock), .Going_down_bullet(movebullet_45_moved_bullet), .Modified_row(r7),
    .Going_up_bullet_2(rowreg_23_going_up_bullet_2), .Tilt_2(rowreg_23_tilt_2),
    .Bounce_2(rowreg_23_bounce_2), .Tilt2(movebullet_45_tilt_2), .Bounce2(movebullet_45_bounce_2),
    .Reset(Reset_t));  // open: gDownSubtract, downHit, gUpSubtract, upHit
  Random #(.width(32), .seed(1115)) random_2 (.clk(Reset_t), .out(random_2_out));  // open: next, clr
  moveBullet movebullet_45 (
    .Bullet(rowreg_24_going_down_bullet_2), .Tilt(rowreg_24_tilt2_2), .Bounce(rowreg_24_bounce2_2),
    .Moved_bullet(movebullet_45_moved_bullet), .Tilt_2(movebullet_45_tilt_2),
    .Bounce_2(movebullet_45_bounce_2));
  Multiplexer #(.width(32), .enable("false")) multiplexer_27 (.in0(r7), .in1({32{1'b0}}), .out(out_16), .sel(all0));
  rowModifier rowmodifier_2 (
    .randomGen(random_2_out), .Reset(Reset_t), .gDownSubtract(rowreg_24_gdownsubtract), .downHit(h3),
    .gUpSubtract(rowreg_24_gupsubtract), .upHit(h4), .out_7(rowmodifier_2_out_7));
  moveBullet movebullet_46 (
    .Bullet(rowreg_23_going_up_bullet_2), .Tilt(rowreg_23_tilt_2), .Bounce(rowreg_23_bounce_2),
    .Moved_bullet(movebullet_46_moved_bullet), .Tilt_2(movebullet_46_tilt_2),
    .Bounce_2(movebullet_46_bounce_2));
  rowReg rowreg_24 (
    .Going_down_bullet_2(rowreg_24_going_down_bullet_2), .Row_values(rowmodifier_2_out_7),
    .Going_up_bullet(movebullet_46_moved_bullet), .Tilt(movebullet_46_tilt_2),
    .Bounce(movebullet_46_bounce_2), .Tilt2_2(rowreg_24_tilt2_2), .Bounce2_2(rowreg_24_bounce2_2),
    .gDownSubtract(rowreg_24_gdownsubtract), .downHit(h3), .Clock(Clock),
    .Going_down_bullet(movebullet_47_moved_bullet), .Modified_row(r6),
    .Going_up_bullet_2(rowreg_24_going_up_bullet_2), .Tilt_2(rowreg_24_tilt_2),
    .Bounce_2(rowreg_24_bounce_2), .Tilt2(movebullet_47_tilt_2), .Bounce2(movebullet_47_bounce_2),
    .gUpSubtract(rowreg_24_gupsubtract), .upHit(h4), .Reset(Reset_t));
  Multiplexer #(.width(32), .enable("false")) multiplexer_28 (.in0(r6), .in1({32{1'b0}}), .out(out_15), .sel(all0));
  moveBullet movebullet_47 (
    .Bullet(rowreg_25_going_down_bullet_2), .Tilt(rowreg_25_tilt2_2), .Bounce(rowreg_25_bounce2_2),
    .Moved_bullet(movebullet_47_moved_bullet), .Tilt_2(movebullet_47_tilt_2),
    .Bounce_2(movebullet_47_bounce_2));
  moveBullet movebullet_48 (
    .Bullet(rowreg_24_going_up_bullet_2), .Tilt(rowreg_24_tilt_2), .Bounce(rowreg_24_bounce_2),
    .Moved_bullet(movebullet_48_moved_bullet), .Tilt_2(movebullet_48_tilt_2),
    .Bounce_2(movebullet_48_bounce_2));
  rowReg rowreg_25 (
    .Going_down_bullet_2(rowreg_25_going_down_bullet_2), .Row_values({32{1'b0}}),
    .Going_up_bullet(movebullet_48_moved_bullet), .Tilt(movebullet_48_tilt_2),
    .Bounce(movebullet_48_bounce_2), .Tilt2_2(rowreg_25_tilt2_2), .Bounce2_2(rowreg_25_bounce2_2),
    .Clock(Clock), .Going_down_bullet(movebullet_49_moved_bullet), .Modified_row(r5),
    .Going_up_bullet_2(rowreg_25_going_up_bullet_2), .Tilt_2(rowreg_25_tilt_2),
    .Bounce_2(rowreg_25_bounce_2), .Tilt2(movebullet_49_tilt_2), .Bounce2(movebullet_49_bounce_2),
    .Reset(Reset_t));  // open: gDownSubtract, downHit, gUpSubtract, upHit
  rowModifier rowmodifier_3 (
    .randomGen(random_3_out), .Reset(Reset_t), .gDownSubtract(rowreg_26_gdownsubtract), .downHit(h5),
    .gUpSubtract(rowreg_26_gupsubtract), .upHit(h6), .out_7(rowmodifier_3_out_7));
  Random #(.width(32), .seed(11117)) random_3 (.clk(Reset_t), .out(random_3_out));  // open: next, clr
  moveBullet movebullet_49 (
    .Bullet(rowreg_26_going_down_bullet_2), .Tilt(rowreg_26_tilt2_2), .Bounce(rowreg_26_bounce2_2),
    .Moved_bullet(movebullet_49_moved_bullet), .Tilt_2(movebullet_49_tilt_2),
    .Bounce_2(movebullet_49_bounce_2));
  moveBullet movebullet_50 (
    .Bullet(rowreg_25_going_up_bullet_2), .Tilt(rowreg_25_tilt_2), .Bounce(rowreg_25_bounce_2),
    .Moved_bullet(movebullet_50_moved_bullet), .Tilt_2(movebullet_50_tilt_2),
    .Bounce_2(movebullet_50_bounce_2));
  Multiplexer #(.width(32), .enable("false")) multiplexer_29 (.in0(r5), .in1({32{1'b0}}), .out(out_14), .sel(all0));
  rowReg rowreg_26 (
    .Going_down_bullet_2(rowreg_26_going_down_bullet_2), .Row_values(rowmodifier_3_out_7),
    .Going_up_bullet(movebullet_50_moved_bullet), .Tilt(movebullet_50_tilt_2),
    .Bounce(movebullet_50_bounce_2), .Tilt2_2(rowreg_26_tilt2_2), .Bounce2_2(rowreg_26_bounce2_2),
    .gDownSubtract(rowreg_26_gdownsubtract), .downHit(h5), .Clock(Clock),
    .Going_down_bullet(movebullet_51_moved_bullet), .Modified_row(r4),
    .Going_up_bullet_2(rowreg_26_going_up_bullet_2), .Tilt_2(rowreg_26_tilt_2),
    .Bounce_2(rowreg_26_bounce_2), .Tilt2(movebullet_51_tilt_2), .Bounce2(movebullet_51_bounce_2),
    .gUpSubtract(rowreg_26_gupsubtract), .upHit(h6), .Reset(Reset_t));
  moveBullet movebullet_51 (
    .Bullet(rowreg_27_going_down_bullet_2), .Tilt(rowreg_27_tilt2_2), .Bounce(rowreg_27_bounce2_2),
    .Moved_bullet(movebullet_51_moved_bullet), .Tilt_2(movebullet_51_tilt_2),
    .Bounce_2(movebullet_51_bounce_2));
  Multiplexer #(.width(32), .enable("false")) multiplexer_30 (.in0(r4), .in1({32{1'b0}}), .out(out_13), .sel(all0));
  moveBullet movebullet_52 (
    .Bullet(rowreg_26_going_up_bullet_2), .Tilt(rowreg_26_tilt_2), .Bounce(rowreg_26_bounce_2),
    .Moved_bullet(movebullet_52_moved_bullet), .Tilt_2(movebullet_52_tilt_2),
    .Bounce_2(movebullet_52_bounce_2));
  Random #(.width(32), .seed(111119)) random_4 (.clk(Reset_t), .out(random_4_out));  // open: next, clr
  rowReg rowreg_27 (
    .Going_down_bullet_2(rowreg_27_going_down_bullet_2), .Row_values({32{1'b0}}),
    .Going_up_bullet(movebullet_52_moved_bullet), .Tilt(movebullet_52_tilt_2),
    .Bounce(movebullet_52_bounce_2), .Tilt2_2(rowreg_27_tilt2_2), .Bounce2_2(rowreg_27_bounce2_2),
    .Clock(Clock), .Going_down_bullet(movebullet_53_moved_bullet), .Modified_row(r3),
    .Going_up_bullet_2(rowreg_27_going_up_bullet_2), .Tilt_2(rowreg_27_tilt_2),
    .Bounce_2(rowreg_27_bounce_2), .Tilt2(movebullet_53_tilt_2), .Bounce2(movebullet_53_bounce_2),
    .Reset(Reset_t));  // open: gDownSubtract, downHit, gUpSubtract, upHit
  Multiplexer #(.width(32), .enable("false")) multiplexer_31 (.in0(r3), .in1({32{1'b0}}), .out(out_12), .sel(all0));
  rowModifier rowmodifier_4 (
    .randomGen(random_4_out), .Reset(Reset_t), .gDownSubtract(rowreg_28_gdownsubtract), .downHit(h7),
    .gUpSubtract(rowreg_28_gupsubtract), .upHit(h8), .out_7(rowmodifier_4_out_7));
  moveBullet movebullet_53 (
    .Bullet(rowreg_28_going_down_bullet_2), .Tilt(rowreg_28_tilt2_2), .Bounce(rowreg_28_bounce2_2),
    .Moved_bullet(movebullet_53_moved_bullet), .Tilt_2(movebullet_53_tilt_2),
    .Bounce_2(movebullet_53_bounce_2));
  moveBullet movebullet_54 (
    .Bullet(rowreg_27_going_up_bullet_2), .Tilt(rowreg_27_tilt_2), .Bounce(rowreg_27_bounce_2),
    .Moved_bullet(movebullet_54_moved_bullet), .Tilt_2(movebullet_54_tilt_2),
    .Bounce_2(movebullet_54_bounce_2));
  rowReg rowreg_28 (
    .Going_down_bullet_2(rowreg_28_going_down_bullet_2), .Row_values(rowmodifier_4_out_7),
    .Going_up_bullet(movebullet_54_moved_bullet), .Tilt(movebullet_54_tilt_2),
    .Bounce(movebullet_54_bounce_2), .Tilt2_2(rowreg_28_tilt2_2), .Bounce2_2(rowreg_28_bounce2_2),
    .gDownSubtract(rowreg_28_gdownsubtract), .downHit(h7), .Clock(Clock),
    .Going_down_bullet(movebullet_55_moved_bullet), .Modified_row(r2),
    .Going_up_bullet_2(rowreg_28_going_up_bullet_2), .Tilt_2(rowreg_28_tilt_2),
    .Bounce_2(rowreg_28_bounce_2), .Tilt2(movebullet_55_tilt_2), .Bounce2(movebullet_55_bounce_2),
    .gUpSubtract(rowreg_28_gupsubtract), .upHit(h8), .Reset(Reset_t));
  moveBullet movebullet_55 (
    .Bullet(rowreg_29_going_down_bullet_2), .Tilt(rowreg_29_tilt2_2), .Bounce(rowreg_29_bounce2_2),
    .Moved_bullet(movebullet_55_moved_bullet), .Tilt_2(movebullet_55_tilt_2),
    .Bounce_2(movebullet_55_bounce_2));
  moveBullet movebullet_56 (
    .Bullet(rowreg_28_going_up_bullet_2), .Tilt(rowreg_28_tilt_2), .Bounce(rowreg_28_bounce_2),
    .Moved_bullet(movebullet_56_moved_bullet), .Tilt_2(movebullet_56_tilt_2),
    .Bounce_2(movebullet_56_bounce_2));
  Multiplexer #(.width(32), .enable("false")) multiplexer_32 (.in0(r2), .in1({32{1'b0}}), .out(out_11), .sel(all0));
  Random #(.width(30), .seed(1111113)) random_5 (.clk(Reset_t), .out(random_5_out));  // open: next, clr
  rowReg rowreg_29 (
    .Going_down_bullet_2(rowreg_29_going_down_bullet_2), .Row_values({32{1'b0}}),
    .Going_up_bullet(movebullet_56_moved_bullet), .Tilt(movebullet_56_tilt_2),
    .Bounce(movebullet_56_bounce_2), .Tilt2_2(rowreg_29_tilt2_2), .Bounce2_2(rowreg_29_bounce2_2),
    .Clock(Clock), .Going_down_bullet(movebullet_57_moved_bullet), .Modified_row(r1),
    .Going_up_bullet_2(rowreg_29_going_up_bullet_2), .Tilt_2(rowreg_29_tilt_2),
    .Bounce_2(rowreg_29_bounce_2), .Tilt2(movebullet_57_tilt_2), .Bounce2(movebullet_57_bounce_2),
    .Reset(Reset_t));  // open: gDownSubtract, downHit, gUpSubtract, upHit
  moveBullet movebullet_57 (
    .Bullet(rowreg_30_going_down_bullet_2), .Tilt(rowreg_30_tilt2_2), .Bounce(rowreg_30_bounce2_2),
    .Moved_bullet(movebullet_57_moved_bullet), .Tilt_2(movebullet_57_tilt_2),
    .Bounce_2(movebullet_57_bounce_2));
  Multiplexer #(.width(32), .enable("false")) multiplexer_33 (.in0(r1), .in1({32{1'b0}}), .out(out_10), .sel(all0));
  rowModifier rowmodifier_5 (
    .randomGen({1'b0, random_5_out, 1'b0}), .Reset(Reset_t), .gDownSubtract(rowreg_30_gdownsubtract),
    .downHit(h9), .gUpSubtract(rowreg_30_gupsubtract), .upHit(h10), .out_7(rowmodifier_5_out_7));
  moveBullet movebullet_58 (
    .Bullet(rowreg_29_going_up_bullet_2), .Tilt(rowreg_29_tilt_2), .Bounce(rowreg_29_bounce_2),
    .Moved_bullet(movebullet_58_moved_bullet), .Tilt_2(movebullet_58_tilt_2),
    .Bounce_2(movebullet_58_bounce_2));
  Comparator #(.width(32)) comparator_3 (.a(r0), .b({32{1'b0}}), .eq(comparator_3_eq));  // open: gt, lt
  Comparator #(.width(32)) comparator_4 (.a(r1), .b({32{1'b0}}), .eq(comparator_4_eq));  // open: gt, lt
  Comparator #(.width(32)) comparator_5 (.a(r2), .b({32{1'b0}}), .eq(comparator_5_eq));  // open: gt, lt
  Comparator #(.width(32)) comparator_6 (.a(r3), .b({32{1'b0}}), .eq(comparator_6_eq));  // open: gt, lt
  Comparator #(.width(32)) comparator_7 (.a(r4), .b({32{1'b0}}), .eq(comparator_7_eq));  // open: gt, lt
  Comparator #(.width(32)) comparator_8 (.a(r5), .b({32{1'b0}}), .eq(comparator_8_eq));  // open: gt, lt
  Comparator #(.width(32)) comparator_9 (.a(r6), .b({32{1'b0}}), .eq(comparator_9_eq));  // open: gt, lt
  Comparator #(.width(32)) comparator_10 (.a(r7), .b({32{1'b0}}), .eq(comparator_10_eq));  // open: gt, lt
  Comparator #(.width(32)) comparator_11 (.a(r8), .b({32{1'b0}}), .eq(comparator_11_eq));  // open: gt, lt
  Comparator #(.width(32)) comparator_12 (.a(r9), .b({32{1'b0}}), .eq(comparator_12_eq));  // open: gt, lt
  Comparator #(.width(32)) comparator_13 (.a(r10), .b({32{1'b0}}), .eq(comparator_13_eq));  // open: gt, lt
  Comparator #(.width(32)) comparator_14 (.a(r11), .b({32{1'b0}}), .eq(comparator_14_eq));  // open: gt, lt
  Comparator #(.width(32)) comparator_15 (.a(r12), .b({32{1'b0}}), .eq(comparator_15_eq));  // open: gt, lt
  Comparator #(.width(32)) comparator_16 (.a(r13), .b({32{1'b0}}), .eq(comparator_16_eq));  // open: gt, lt
  Comparator #(.width(32)) comparator_17 (.a(r14), .b({32{1'b0}}), .eq(comparator_17_eq));  // open: gt, lt
  Comparator #(.width(32)) comparator_18 (.a(r15), .b({32{1'b0}}), .eq(comparator_18_eq));  // open: gt, lt
  Comparator #(.width(32)) comparator_19 (.a(r16), .b({32{1'b0}}), .eq(comparator_19_eq));  // open: gt, lt
  Comparator #(.width(32)) comparator_20 (.a(r17), .b({32{1'b0}}), .eq(comparator_20_eq));  // open: gt, lt
  Comparator #(.width(32)) comparator_21 (.a(r18), .b({32{1'b0}}), .eq(comparator_21_eq));  // open: gt, lt
  Comparator #(.width(32)) comparator_22 (.a(r19), .b({32{1'b0}}), .eq(comparator_22_eq));  // open: gt, lt
  Comparator #(.width(32)) comparator_23 (.a(r20), .b({32{1'b0}}), .eq(comparator_23_eq));  // open: gt, lt
  Comparator #(.width(32)) comparator_24 (.a(r21), .b({32{1'b0}}), .eq(comparator_24_eq));  // open: gt, lt
  Comparator #(.width(32)) comparator_25 (.a(r22), .b({32{1'b0}}), .eq(comparator_25_eq));  // open: gt, lt
  Comparator #(.width(32)) comparator_26 (.a(r23), .b({32{1'b0}}), .eq(comparator_26_eq));  // open: gt, lt
  Comparator #(.width(32)) comparator_27 (.a(r24), .b({32{1'b0}}), .eq(comparator_27_eq));  // open: gt, lt
  Comparator #(.width(32)) comparator_28 (.a(r25), .b({32{1'b0}}), .eq(comparator_28_eq));  // open: gt, lt
  Comparator #(.width(32)) comparator_29 (.a(r26), .b({32{1'b0}}), .eq(comparator_29_eq));  // open: gt, lt
  Comparator #(.width(32)) comparator_30 (.a(r27), .b({32{1'b0}}), .eq(comparator_30_eq));  // open: gt, lt
  Comparator #(.width(32)) comparator_31 (.a(r28), .b({32{1'b0}}), .eq(comparator_31_eq));  // open: gt, lt
  Comparator #(.width(32)) comparator_32 (.a(r29), .b({32{1'b0}}), .eq(comparator_32_eq));  // open: gt, lt
  rowReg rowreg_30 (
    .Going_down_bullet_2(rowreg_30_going_down_bullet_2), .Row_values(rowmodifier_5_out_7),
    .Going_up_bullet(movebullet_58_moved_bullet), .Tilt(movebullet_58_tilt_2),
    .Bounce(movebullet_58_bounce_2), .Tilt2_2(rowreg_30_tilt2_2), .Bounce2_2(rowreg_30_bounce2_2),
    .gDownSubtract(rowreg_30_gdownsubtract), .downHit(h9), .Clock(Clock),
    .Going_down_bullet(movebullet_59_moved_bullet), .Modified_row(r0),
    .Going_up_bullet_2(rowreg_30_going_up_bullet_2), .Tilt_2(rowreg_30_tilt_2),
    .Bounce_2(rowreg_30_bounce_2), .Tilt2(movebullet_59_tilt_2), .Bounce2(movebullet_59_bounce_2),
    .gUpSubtract(rowreg_30_gupsubtract), .upHit(h10), .Reset(Reset_t));
  moveBullet movebullet_59 (
    .Bullet(rowreg_30_going_up_bullet_2), .Tilt(rowreg_30_tilt_2), .Bounce(rowreg_30_bounce_2),
    .Moved_bullet(movebullet_59_moved_bullet), .Tilt_2(movebullet_59_tilt_2),
    .Bounce_2(movebullet_59_bounce_2));
  Multiplexer #(.width(32), .enable("false")) multiplexer_34 (.in0(r0), .in1({32{1'b0}}), .out(out_9), .sel(all0));
  score score_1 (.out_3(score1), .out_4(score0), .in_1(or_2_out), .in_2(Reset_t));
  or or_2 (or_2_out, h1, h2, h3, h4, h5, h6, h7, h8, h9, h10);
  and and_1 (and_1_out, comparator_3_eq, comparator_4_eq, comparator_5_eq, comparator_6_eq, comparator_7_eq, comparator_8_eq, comparator_9_eq, comparator_10_eq, comparator_11_eq, comparator_12_eq, comparator_13_eq, comparator_14_eq, comparator_15_eq, comparator_16_eq, comparator_17_eq, comparator_18_eq, comparator_19_eq, comparator_20_eq, comparator_21_eq, comparator_22_eq, comparator_23_eq, comparator_24_eq, comparator_25_eq, comparator_26_eq, comparator_27_eq, comparator_28_eq, comparator_29_eq, comparator_30_eq, comparator_31_eq, comparator_32_eq);
  or or_3 (all0, and_1_out, lose);

  // Notes on the sheet:
  //   Bounce initial value
endmodule

module rowCompare (
  input  [31:0] rowValue,
  input  [31:0] bulletPos,
  input  Bounce,
  output [31:0] rowValue_2,
  output [31:0] bulletPos_2,
  output Hit
);

  wire comparator_1_eq, comparator_2_eq, comparator_3_eq, comparator_4_eq, comparator_5_eq, comparator_6_eq,
       comparator_7_eq, comparator_8_eq, comparator_9_eq, comparator_10_eq, comparator_11_eq,
       comparator_12_eq, comparator_13_eq, comparator_14_eq, comparator_15_eq, comparator_16_eq,
       comparator_17_eq, comparator_18_eq, comparator_19_eq, comparator_20_eq, comparator_21_eq,
       comparator_22_eq, comparator_23_eq, comparator_24_eq, comparator_25_eq, comparator_26_eq,
       comparator_27_eq, comparator_28_eq, comparator_29_eq, comparator_30_eq, comparator_31_eq,
       comparator_32_eq, comparator_33_eq, comparator_34_eq, comparator_35_eq, comparator_36_eq,
       comparator_37_eq, comparator_38_eq, comparator_39_eq, comparator_40_eq, comparator_41_eq,
       comparator_42_eq, comparator_43_eq, comparator_44_eq, comparator_45_eq, comparator_46_eq,
       comparator_47_eq, comparator_48_eq, comparator_49_eq, comparator_50_eq, comparator_51_eq,
       comparator_52_eq, comparator_53_eq, comparator_54_eq, comparator_55_eq, comparator_56_eq,
       comparator_57_eq, comparator_58_eq, comparator_59_eq, comparator_60_eq, comparator_61_eq,
       comparator_62_eq, comparator_63_eq, comparator_64_eq, O0, O1, O2, O3, O4, O5, O6, O7, O8, O9, O10,
       O11, O12, O13, O14, O15, O16, O17, O18, O19, O20, O21, O22, O23, O24, O25, O26, O27, O28, O29, O30,
       O31, xor_1_out;

  Comparator #(.width(1)) comparator_1 (.a(bulletPos[0]), .b(1'b1), .eq(comparator_1_eq));  // open: gt, lt
  and and_1 (O0, comparator_1_eq, comparator_2_eq);
  Comparator #(.width(1)) comparator_2 (.a(rowValue[0]), .b(1'b1), .eq(comparator_2_eq));  // open: gt, lt
  Comparator #(.width(1)) comparator_3 (.a(bulletPos[1]), .b(1'b1), .eq(comparator_3_eq));  // open: gt, lt
  and and_2 (O1, comparator_3_eq, comparator_4_eq);
  Comparator #(.width(1)) comparator_4 (.a(rowValue[1]), .b(1'b1), .eq(comparator_4_eq));  // open: gt, lt
  Comparator #(.width(1)) comparator_5 (.a(bulletPos[2]), .b(1'b1), .eq(comparator_5_eq));  // open: gt, lt
  and and_3 (O2, comparator_5_eq, comparator_6_eq);
  Comparator #(.width(1)) comparator_6 (.a(rowValue[2]), .b(1'b1), .eq(comparator_6_eq));  // open: gt, lt
  Comparator #(.width(1)) comparator_7 (.a(bulletPos[3]), .b(1'b1), .eq(comparator_7_eq));  // open: gt, lt
  and and_4 (O3, comparator_7_eq, comparator_8_eq);
  Comparator #(.width(1)) comparator_8 (.a(rowValue[3]), .b(1'b1), .eq(comparator_8_eq));  // open: gt, lt
  Comparator #(.width(1)) comparator_9 (.a(bulletPos[4]), .b(1'b1), .eq(comparator_9_eq));  // open: gt, lt
  and and_5 (O4, comparator_9_eq, comparator_10_eq);
  Comparator #(.width(1)) comparator_10 (.a(rowValue[4]), .b(1'b1), .eq(comparator_10_eq));  // open: gt, lt
  Comparator #(.width(1)) comparator_11 (.a(bulletPos[5]), .b(1'b1), .eq(comparator_11_eq));  // open: gt, lt
  and and_6 (O5, comparator_11_eq, comparator_12_eq);
  Comparator #(.width(1)) comparator_12 (.a(rowValue[5]), .b(1'b1), .eq(comparator_12_eq));  // open: gt, lt
  Comparator #(.width(1)) comparator_13 (.a(bulletPos[6]), .b(1'b1), .eq(comparator_13_eq));  // open: gt, lt
  and and_7 (O6, comparator_13_eq, comparator_14_eq);
  Comparator #(.width(1)) comparator_14 (.a(rowValue[6]), .b(1'b1), .eq(comparator_14_eq));  // open: gt, lt
  Comparator #(.width(1)) comparator_15 (.a(bulletPos[7]), .b(1'b1), .eq(comparator_15_eq));  // open: gt, lt
  and and_8 (O7, comparator_15_eq, comparator_16_eq);
  Comparator #(.width(1)) comparator_16 (.a(rowValue[7]), .b(1'b1), .eq(comparator_16_eq));  // open: gt, lt
  Comparator #(.width(1)) comparator_17 (.a(bulletPos[8]), .b(1'b1), .eq(comparator_17_eq));  // open: gt, lt
  Comparator #(.width(1)) comparator_18 (.a(rowValue[8]), .b(1'b1), .eq(comparator_18_eq));  // open: gt, lt
  Comparator #(.width(1)) comparator_19 (.a(bulletPos[9]), .b(1'b1), .eq(comparator_19_eq));  // open: gt, lt
  Comparator #(.width(1)) comparator_20 (.a(rowValue[9]), .b(1'b1), .eq(comparator_20_eq));  // open: gt, lt
  Comparator #(.width(1)) comparator_21 (.a(bulletPos[10]), .b(1'b1), .eq(comparator_21_eq));  // open: gt, lt
  Comparator #(.width(1)) comparator_22 (.a(rowValue[10]), .b(1'b1), .eq(comparator_22_eq));  // open: gt, lt
  Comparator #(.width(1)) comparator_23 (.a(bulletPos[11]), .b(1'b1), .eq(comparator_23_eq));  // open: gt, lt
  Comparator #(.width(1)) comparator_24 (.a(rowValue[11]), .b(1'b1), .eq(comparator_24_eq));  // open: gt, lt
  Comparator #(.width(1)) comparator_25 (.a(bulletPos[12]), .b(1'b1), .eq(comparator_25_eq));  // open: gt, lt
  Comparator #(.width(1)) comparator_26 (.a(rowValue[12]), .b(1'b1), .eq(comparator_26_eq));  // open: gt, lt
  Comparator #(.width(1)) comparator_27 (.a(bulletPos[13]), .b(1'b1), .eq(comparator_27_eq));  // open: gt, lt
  Comparator #(.width(1)) comparator_28 (.a(rowValue[13]), .b(1'b1), .eq(comparator_28_eq));  // open: gt, lt
  Comparator #(.width(1)) comparator_29 (.a(bulletPos[14]), .b(1'b1), .eq(comparator_29_eq));  // open: gt, lt
  Comparator #(.width(1)) comparator_30 (.a(rowValue[14]), .b(1'b1), .eq(comparator_30_eq));  // open: gt, lt
  Comparator #(.width(1)) comparator_31 (.a(bulletPos[15]), .b(1'b1), .eq(comparator_31_eq));  // open: gt, lt
  Comparator #(.width(1)) comparator_32 (.a(rowValue[15]), .b(1'b1), .eq(comparator_32_eq));  // open: gt, lt
  and and_9 (O8, comparator_17_eq, comparator_18_eq);
  and and_10 (O9, comparator_19_eq, comparator_20_eq);
  and and_11 (O10, comparator_21_eq, comparator_22_eq);
  and and_12 (O11, comparator_23_eq, comparator_24_eq);
  and and_13 (O12, comparator_25_eq, comparator_26_eq);
  and and_14 (O13, comparator_27_eq, comparator_28_eq);
  and and_15 (O14, comparator_29_eq, comparator_30_eq);
  and and_16 (O15, comparator_31_eq, comparator_32_eq);
  Comparator #(.width(1)) comparator_33 (.a(bulletPos[16]), .b(1'b1), .eq(comparator_33_eq));  // open: gt, lt
  Comparator #(.width(1)) comparator_34 (.a(rowValue[16]), .b(1'b1), .eq(comparator_34_eq));  // open: gt, lt
  Comparator #(.width(1)) comparator_35 (.a(bulletPos[17]), .b(1'b1), .eq(comparator_35_eq));  // open: gt, lt
  Comparator #(.width(1)) comparator_36 (.a(rowValue[17]), .b(1'b1), .eq(comparator_36_eq));  // open: gt, lt
  Comparator #(.width(1)) comparator_37 (.a(bulletPos[18]), .b(1'b1), .eq(comparator_37_eq));  // open: gt, lt
  Comparator #(.width(1)) comparator_38 (.a(rowValue[18]), .b(1'b1), .eq(comparator_38_eq));  // open: gt, lt
  Comparator #(.width(1)) comparator_39 (.a(bulletPos[19]), .b(1'b1), .eq(comparator_39_eq));  // open: gt, lt
  Comparator #(.width(1)) comparator_40 (.a(rowValue[19]), .b(1'b1), .eq(comparator_40_eq));  // open: gt, lt
  Comparator #(.width(1)) comparator_41 (.a(bulletPos[20]), .b(1'b1), .eq(comparator_41_eq));  // open: gt, lt
  Comparator #(.width(1)) comparator_42 (.a(rowValue[20]), .b(1'b1), .eq(comparator_42_eq));  // open: gt, lt
  Comparator #(.width(1)) comparator_43 (.a(bulletPos[21]), .b(1'b1), .eq(comparator_43_eq));  // open: gt, lt
  Comparator #(.width(1)) comparator_44 (.a(rowValue[21]), .b(1'b1), .eq(comparator_44_eq));  // open: gt, lt
  Comparator #(.width(1)) comparator_45 (.a(bulletPos[22]), .b(1'b1), .eq(comparator_45_eq));  // open: gt, lt
  Comparator #(.width(1)) comparator_46 (.a(rowValue[22]), .b(1'b1), .eq(comparator_46_eq));  // open: gt, lt
  Comparator #(.width(1)) comparator_47 (.a(bulletPos[23]), .b(1'b1), .eq(comparator_47_eq));  // open: gt, lt
  Comparator #(.width(1)) comparator_48 (.a(rowValue[23]), .b(1'b1), .eq(comparator_48_eq));  // open: gt, lt
  and and_17 (O16, comparator_33_eq, comparator_34_eq);
  and and_18 (O17, comparator_35_eq, comparator_36_eq);
  and and_19 (O18, comparator_37_eq, comparator_38_eq);
  and and_20 (O19, comparator_39_eq, comparator_40_eq);
  and and_21 (O20, comparator_41_eq, comparator_42_eq);
  and and_22 (O21, comparator_43_eq, comparator_44_eq);
  and and_23 (O22, comparator_45_eq, comparator_46_eq);
  and and_24 (O23, comparator_47_eq, comparator_48_eq);
  Comparator #(.width(1)) comparator_49 (.a(bulletPos[24]), .b(1'b1), .eq(comparator_49_eq));  // open: gt, lt
  Comparator #(.width(1)) comparator_50 (.a(rowValue[24]), .b(1'b1), .eq(comparator_50_eq));  // open: gt, lt
  Comparator #(.width(1)) comparator_51 (.a(bulletPos[25]), .b(1'b1), .eq(comparator_51_eq));  // open: gt, lt
  Comparator #(.width(1)) comparator_52 (.a(rowValue[25]), .b(1'b1), .eq(comparator_52_eq));  // open: gt, lt
  Comparator #(.width(1)) comparator_53 (.a(bulletPos[26]), .b(1'b1), .eq(comparator_53_eq));  // open: gt, lt
  Comparator #(.width(1)) comparator_54 (.a(rowValue[26]), .b(1'b1), .eq(comparator_54_eq));  // open: gt, lt
  Comparator #(.width(1)) comparator_55 (.a(bulletPos[27]), .b(1'b1), .eq(comparator_55_eq));  // open: gt, lt
  Comparator #(.width(1)) comparator_56 (.a(rowValue[27]), .b(1'b1), .eq(comparator_56_eq));  // open: gt, lt
  Comparator #(.width(1)) comparator_57 (.a(bulletPos[28]), .b(1'b1), .eq(comparator_57_eq));  // open: gt, lt
  Comparator #(.width(1)) comparator_58 (.a(rowValue[28]), .b(1'b1), .eq(comparator_58_eq));  // open: gt, lt
  Comparator #(.width(1)) comparator_59 (.a(bulletPos[29]), .b(1'b1), .eq(comparator_59_eq));  // open: gt, lt
  Comparator #(.width(1)) comparator_60 (.a(rowValue[29]), .b(1'b1), .eq(comparator_60_eq));  // open: gt, lt
  Comparator #(.width(1)) comparator_61 (.a(bulletPos[30]), .b(1'b1), .eq(comparator_61_eq));  // open: gt, lt
  Comparator #(.width(1)) comparator_62 (.a(rowValue[30]), .b(1'b1), .eq(comparator_62_eq));  // open: gt, lt
  Comparator #(.width(1)) comparator_63 (.a(bulletPos[31]), .b(1'b1), .eq(comparator_63_eq));  // open: gt, lt
  Comparator #(.width(1)) comparator_64 (.a(rowValue[31]), .b(1'b1), .eq(comparator_64_eq));  // open: gt, lt
  and and_25 (O24, comparator_49_eq, comparator_50_eq);
  and and_26 (O25, comparator_51_eq, comparator_52_eq);
  and and_27 (O26, comparator_53_eq, comparator_54_eq);
  and and_28 (O27, comparator_55_eq, comparator_56_eq);
  and and_29 (O28, comparator_57_eq, comparator_58_eq);
  and and_30 (O29, comparator_59_eq, comparator_60_eq);
  and and_31 (O30, comparator_61_eq, comparator_62_eq);
  and and_32 (O31, comparator_63_eq, comparator_64_eq);
  xor xor_1 (xor_1_out, O0, O1, O2, O3, O4, O5, O6, O7, O8, O9, O10, O11, O12, O13, O14, O15, O16, O17, O18, O19, O20, O21, O22, O23, O24, O25, O26, O27, O28, O29, O30, O31);
  and and_33 (Hit, xor_1_out, Bounce);
  Multiplexer #(.width(32), .enable("false")) multiplexer_1 (
    .in0({32{1'b0}}), .in1(bulletPos), .out(rowValue_2), .sel(Hit));
  Multiplexer #(.width(32), .enable("false")) multiplexer_2 (
    .in0(bulletPos), .in1({32{1'b0}}), .out(bulletPos_2), .sel(Hit));

  // Other names for the same wires on the sheet: B0 = bulletPos[0]; B1 = bulletPos[1]; B2 = bulletPos[2];
  //   B3 = bulletPos[3]; B4 = bulletPos[4]; B5 = bulletPos[5]; B6 = bulletPos[6]; B7 = bulletPos[7];
  //   B8 = bulletPos[8]; B9 = bulletPos[9]; B10 = bulletPos[10]; B11 = bulletPos[11]; B12 = bulletPos[12];
  //   B13 = bulletPos[13]; B14 = bulletPos[14]; B15 = bulletPos[15]; B16 = bulletPos[16]; B17 = bulletPos[17];
  //   B18 = bulletPos[18]; B19 = bulletPos[19]; B20 = bulletPos[20]; B21 = bulletPos[21]; B22 = bulletPos[22];
  //   B23 = bulletPos[23]; B24 = bulletPos[24]; B25 = bulletPos[25]; B26 = bulletPos[26]; B27 = bulletPos[27];
  //   B28 = bulletPos[28]; B29 = bulletPos[29]; B30 = bulletPos[30]; B31 = bulletPos[31]; R0 = rowValue[0];
  //   R1 = rowValue[1]; R2 = rowValue[2]; R3 = rowValue[3]; R4 = rowValue[4]; R5 = rowValue[5]; R6 = rowValue[6];
  //   R7 = rowValue[7]; R8 = rowValue[8]; R9 = rowValue[9]; R10 = rowValue[10]; R11 = rowValue[11];
  //   R12 = rowValue[12]; R13 = rowValue[13]; R14 = rowValue[14]; R15 = rowValue[15]; R16 = rowValue[16];
  //   R17 = rowValue[17]; R18 = rowValue[18]; R19 = rowValue[19]; R20 = rowValue[20]; R21 = rowValue[21];
  //   R22 = rowValue[22]; R23 = rowValue[23]; R24 = rowValue[24]; R25 = rowValue[25]; R26 = rowValue[26];
  //   R27 = rowValue[27]; R28 = rowValue[28]; R29 = rowValue[29]; R30 = rowValue[30]; R31 = rowValue[31]
endmodule

module rowModifier (
  input  [31:0] gUpSubtract,
  input  [31:0] randomGen,
  input  upHit,
  input  Reset,
  input  [31:0] gDownSubtract,
  input  downHit,
  output [31:0] out_7
);

  wire xor_2_out;
  wire [31:0] multiplexer_1_out, xor_1_out;

  Multiplexer #(.width(32), .enable("false")) multiplexer_1 (
    .in0(out_7), .in1(randomGen), .out(multiplexer_1_out), .sel(Reset));
  assign xor_1_out = multiplexer_1_out ^ gUpSubtract ^ gDownSubtract;  // XOR_Gate xor_1, 32 bits wide
  Register #(.width(32), .trigger("falling")) register_1 (.D(xor_1_out), .Q(out_7), .clk(xor_2_out));  // open: en, clr
  xor xor_2 (xor_2_out, Reset, downHit, upHit);
endmodule

module score (
  input  in_1,
  input  in_2,
  output [3:0] out_3,
  output [3:0] out_4
);

  wire comparator_1_eq, or_1_out;

  Counter #(.width(4), .max('hf)) counter_1 (.Q(out_4), .clk(in_1), .clr(or_1_out));  // open: load, D, count, carry
  Comparator #(.width(4)) comparator_1 (.a(out_4), .b(4'b1010), .eq(comparator_1_eq));  // open: gt, lt
  or or_1 (or_1_out, comparator_1_eq, in_2);
  Counter #(.width(4), .max('hf)) counter_2 (
    .Q(out_3), .clk(comparator_1_eq), .clr(in_2));  // open: load, D, count, carry
endmodule

module cannonHit (
  input  [31:0] cannonPos,
  input  [31:0] bulletPos,
  input  [31:0] basePos,
  input  Tilt,
  output out_5
);

  wire comparator_1_eq, comparator_2_eq, comparator_3_eq, comparator_4_eq, comparator_5_eq, comparator_6_eq,
       comparator_7_eq, comparator_8_eq, or_1_out, or_2_out;
  wire [31:0] shifter_1_out, shifter_2_out, shifter_3_out, shifter_4_out;

  Shifter #(.width(32)) shifter_1 (.in(bulletPos), .\dist (5'b00001), .out(shifter_1_out));
  Shifter #(.width(32)) shifter_2 (.in(bulletPos), .\dist (5'b00010), .out(shifter_2_out));
  Shifter #(.width(32), .shift("lr")) shifter_3 (.in(bulletPos), .\dist (5'b00001), .out(shifter_3_out));
  Shifter #(.width(32), .shift("lr")) shifter_4 (.in(bulletPos), .\dist (5'b00010), .out(shifter_4_out));
  Comparator #(.width(32)) comparator_1 (.a(cannonPos), .b(shifter_1_out), .eq(comparator_1_eq));  // open: gt, lt
  Comparator #(.width(32)) comparator_2 (.a(cannonPos), .b(shifter_2_out), .eq(comparator_2_eq));  // open: gt, lt
  Comparator #(.width(32)) comparator_3 (.a(basePos), .b(shifter_1_out), .eq(comparator_3_eq));  // open: gt, lt
  Comparator #(.width(32)) comparator_4 (.a(basePos), .b(shifter_2_out), .eq(comparator_4_eq));  // open: gt, lt
  Comparator #(.width(32)) comparator_5 (.a(cannonPos), .b(shifter_3_out), .eq(comparator_5_eq));  // open: gt, lt
  Comparator #(.width(32)) comparator_6 (.a(cannonPos), .b(shifter_4_out), .eq(comparator_6_eq));  // open: gt, lt
  Comparator #(.width(32)) comparator_7 (.a(basePos), .b(shifter_3_out), .eq(comparator_7_eq));  // open: gt, lt
  Comparator #(.width(32)) comparator_8 (.a(basePos), .b(shifter_4_out), .eq(comparator_8_eq));  // open: gt, lt
  or or_1 (or_1_out, comparator_1_eq, comparator_2_eq, comparator_3_eq, comparator_4_eq);
  or or_2 (or_2_out, comparator_5_eq, comparator_6_eq, comparator_7_eq, comparator_8_eq);
  Multiplexer #(.enable("false")) multiplexer_1 (.in0(or_2_out), .in1(or_1_out), .out(out_5), .sel(Tilt));
endmodule
